// Logisim project processor.circ as structural Verilog: 17 circuits, main circuit main
module main (
  input  reset
);

  wire alu_1_ovf, and_2_out, clk, CLR_D, CLR_F, CLR_X, CTRL_RECOVERY, D_CTRL_F_RD_OK, D_CTRL_F_RS_OK,
       D_CTRL_RD_OK, D_CTRL_RECOVERY, D_CTRL_RS_OK, D_JAL, D_LW, D_RESOLVE_RD_out_valid,
       D_RESOLVE_RS_out_valid, D_SETX, eq5_1_out, eq5_2_out, eq5_3_out, eq5_4_out, eq5_5_out, eq5_6_out,
       eq5_7_out, eq5_11_out, eq5_12_out, eq5_13_out, eq5_16_out, eq5_17_out, eq5_19_out, eq5_20_out,
       eq5_21_out, F_ADD, F_CTRL_RD_OK, F_CTRL_RECOVERY, F_CTRL_RS_OK, F_JUMP, F_RESOLVE_RD_out_valid,
       F_RESOLVE_RS_out_valid, F_STALL, M_CTRL_D_RD_OK, M_CTRL_D_RS_OK, M_CTRL_F_RD_OK, M_CTRL_F_RS_OK,
       M_CTRL_X_RD_OK, M_CTRL_X_RS_OK, M_LW, M_RES_VALID, M_RESOLVE, M_SW, M_VAL1_valid_out,
       M_VAL2_valid_out, nor_1_out, not_1_out, or_3_out, or_4_out, or_8_out, or_9_out, or_10_out, or_11_out,
       or_12_out, or_13_out, or_15_out, or_17_out, W_CTRL_F_RD_CHECK_ok, W_CTRL_F_RS_CHECK_ok, W_RES_VALID,
       X_ADDI, X_ALUOP_HDEC, X_CACHE_RD_valid_out, X_CACHE_RS_valid_out, X_CTRL_D_RD_OK, X_CTRL_D_RS_OK,
       X_CTRL_F_RD_OK, X_CTRL_F_RS_OK, X_GEN_EXC, X_JAL, X_RES_VALID, X_RESOLVE_RD_out_valid,
       X_RESOLVE_RS_out_valid, X_SETX, X_VAL2_valid_out;
  wire [1:0] priority_encoder_1_out;
  wire [4:0] D_CTRL_RD, D_CTRL_RS, D_INSN_DEC_opcode, D_INSN_DEC_rd, D_INSN_DEC_rt, F_CTRL_RD, F_CTRL_RS,
       F_CTRL_RT, F_INSN_DEC_opcode, F_INSN_DEC_rd, M_INSN_DEC_opcode, M_RD, M_RES_ID, M_VAL1_id_out,
       M_VAL2_id_out, multiplexer_15_out, multiplexer_16_out, W_INSN_DEC_opcode, W_RES_ID, X_ALUOP,
       X_CACHE_RD_id_out, X_CACHE_RS_id_out, X_CTRL_RD, X_CTRL_RS, X_INSN_DEC_aluop, X_INSN_DEC_opcode,
       X_RES_ID, X_SHAMT, X_VAL2_id_out;
  wire [11:0] bit_extender_4_out;
  wire [16:0] M_IMM, X_INSN_DEC_imm;
  wire [26:0] D_INSN_DEC_target, F_INSN_DEC_target;
  wire [31:0] alu_1_out_7, bit_extender_5_out, CTRL_NEXT_PC, D_CTRL_NEXT_PC, D_FILTERED_RD, D_FILTERED_RS,
       D_INSN, D_PC, D_RES_RD, D_RES_RS, D_RESOLVE_RD_out_data, D_RESOLVE_RS_out_data, D_TARGET,
       F_CTRL_NEXT_PC, F_INSN, F_PC, F_RESOLVE_RD_out_data, F_RESOLVE_RS_out_data, F_TARGET, M_INSN, M_RES,
       M_RESOLVED_ADDR, M_RESOLVED_DATA, M_VAL1_data_out, M_VAL2_data_out, multiplexer_1_out,
       multiplexer_2_out, multiplexer_3_out, multiplexer_5_out, multiplexer_7_out, multiplexer_9_out,
       multiplexer_10_out, multiplexer_11_out, multiplexer_12_out, multiplexer_13_out, multiplexer_18_out,
       multiplexer_19_out, multiplexer_20_out, multiplexer_22_out, multiplexer_23_out,
       n32_bit_compact_1_result, ram_1_data, W_INSN, writeback_selector_1_data_out,
       writeback_selector_2_data_out, writeback_selector_3_data_out, writeback_selector_4_data_out,
       writeback_selector_7_data_out, writeback_selector_8_data_out, X_CACHE_RD_data_out,
       X_CACHE_RS_data_out, X_CTRL_NEXT_PC, X_IMM, X_INSN, X_PC, X_RES, X_RESOLVE_RD_out_data,
       X_RESOLVE_RS_out_data, X_VAL1_data_out, X_VAL2_data_out;

  Multiplexer #(.width(32), .disabled(0), .enable("false")) multiplexer_1 (
    .in0(n32_bit_compact_1_result), .in1(F_PC), .out(multiplexer_1_out), .sel(F_STALL));
  Multiplexer #(.width(32), .disabled(0), .enable("false")) multiplexer_2 (
    .in0(multiplexer_1_out), .in1(F_TARGET), .out(multiplexer_2_out), .sel(F_JUMP));
  Multiplexer #(.width(32), .disabled(0), .enable("false")) multiplexer_3 (
    .in0(multiplexer_2_out), .in1(CTRL_NEXT_PC), .out(multiplexer_3_out), .sel(CTRL_RECOVERY));
  insn_decoder F_INSN_DEC (
    .insn(F_INSN), .target(F_INSN_DEC_target), .opcode(F_INSN_DEC_opcode), .rd(F_INSN_DEC_rd),
    .rs(F_CTRL_RS), .rt(F_CTRL_RT));  // open: aluop, imm, shamt
  // Probe on F_PC
  register_32 PC (.clk(clk), .\input (multiplexer_3_out), .enable(1'b1), .\output (F_PC), .reset(reset));
  eq5 eq5_1 (.in1(F_INSN_DEC_opcode), .in2(5'b00101), .out(eq5_1_out));
  eq5 eq5_2 (.in1(F_INSN_DEC_opcode), .in2({5{1'b0}}), .out(eq5_2_out));
  eq5 eq5_3 (.in1(F_INSN_DEC_opcode), .in2(5'b00011), .out(eq5_3_out));
  eq5 eq5_4 (.in1(F_INSN_DEC_opcode), .in2(5'b00001), .out(eq5_4_out));
  assign F_TARGET = {{5{1'b0}}, F_INSN_DEC_target};  // Bit_Extender bit_extender_1
  _32_bit_compact u_32_bit_compact_1 (.result(n32_bit_compact_1_result), .A(32'h1), .B(F_PC), .sub(1'b0));  // open: ovf
  eq5 eq5_5 (.in1(F_CTRL_RS), .in2(D_CTRL_RD), .out(eq5_5_out));
  eq5 eq5_6 (.in1(D_CTRL_RD), .in2(F_CTRL_RT), .out(eq5_6_out));
  or or_1 (F_ADD, eq5_1_out, eq5_2_out);
  or or_2 (F_JUMP, eq5_3_out, eq5_4_out);
  register_32 u_D_PC (.clk(clk), .\input (F_PC), .enable(1'b1), .\output (D_PC), .reset(reset));
  or or_3 (or_3_out, eq5_5_out, eq5_6_out);
  register_resolver F_RESOLVE_RD (
    .reg_id(F_CTRL_RD), .in0_valid(W_RES_VALID), .in0_id(W_RES_ID), .in1_valid(M_RES_VALID),
    .in1_id(M_RES_ID), .in2_valid(X_RES_VALID), .in2_id(X_RES_ID), .in3_valid(1'b1), .in3_id(D_CTRL_RD),
    .in0_data(M_RESOLVED_DATA), .in1_data(M_RES), .in2_data(X_RES), .in3_data(D_FILTERED_RD),
    .out_valid(F_RESOLVE_RD_out_valid), .out_data(F_RESOLVE_RD_out_data));
  register_resolver F_RESOLVE_RS (
    .reg_id(F_CTRL_RS), .in0_valid(W_RES_VALID), .in0_id(W_RES_ID), .in1_valid(M_RES_VALID),
    .in1_id(M_RES_ID), .in2_valid(X_RES_VALID), .in2_id(X_RES_ID), .in3_valid(1'b1), .in3_id(D_CTRL_RS),
    .in0_data(M_RESOLVED_DATA), .in1_data(M_RES), .in2_data(X_RES), .in3_data(D_FILTERED_RS),
    .out_valid(F_RESOLVE_RS_out_valid), .out_data(F_RESOLVE_RS_out_data));
  eq5 eq5_7 (.in1(F_INSN_DEC_opcode), .in2(5'b10110), .out(eq5_7_out));
  Multiplexer #(.width(5), .disabled(0), .enable("false")) multiplexer_4 (
    .in0(F_INSN_DEC_rd), .in1(5'b11110), .out(F_CTRL_RD), .sel(eq5_7_out));
  register_32 u_X_PC (.clk(clk), .\input (D_PC), .enable(1'b1), .\output (X_PC), .reset(reset));
  ROM #(.addrWidth(12), .dataWidth(32)) rom_1 (.addr(F_PC[11:0]), .data(F_INSN), .sel(1'b1));
  Multiplexer #(.width(32), .disabled(0), .enable("false")) multiplexer_5 (
    .in0(F_INSN), .in1({32{1'b0}}), .out(multiplexer_5_out), .sel(or_4_out));
  and and_1 (F_STALL, D_LW, F_ADD, or_3_out);
  register_32 u_D_INSN (.clk(clk), .\input (multiplexer_5_out), .enable(1'b1), .\output (D_INSN), .reset(reset));
  or or_4 (or_4_out, CLR_F, F_STALL);
  branch_resolver F_RESOLVE_CTRL (
    .insn(F_INSN), .pc(F_PC), .rd_no_conflicts(F_CTRL_RD_OK), .rd_valid(F_RESOLVE_RD_out_valid),
    .rd_data(F_RESOLVE_RD_out_data), .rs_valid(F_RESOLVE_RS_out_valid), .rs_data(F_RESOLVE_RS_out_data),
    .recovery(F_CTRL_RECOVERY), .next_pc(F_CTRL_NEXT_PC), .rs_no_conflicts(F_CTRL_RS_OK));
  Clock clock_1 (.out(clk));
  insn_decoder D_INSN_DEC (
    .insn(D_INSN), .target(D_INSN_DEC_target), .opcode(D_INSN_DEC_opcode), .rd(D_INSN_DEC_rd),
    .rs(D_CTRL_RS), .rt(D_INSN_DEC_rt));  // open: aluop, imm, shamt
  stage_resolution_checker D_CTRL_F_RD_CHECK (
    .insn(D_INSN), .\reg (F_CTRL_RD), .stage_has_resolved_arith(1'b0), .stage_has_resolved_lw(1'b0),
    .ok(D_CTRL_F_RD_OK));
  stage_resolution_checker D_CTRL_F_RS_CHECK (
    .insn(D_INSN), .\reg (F_CTRL_RS), .stage_has_resolved_arith(1'b0), .stage_has_resolved_lw(1'b0),
    .ok(D_CTRL_F_RS_OK));
  Multiplexer #(.select(5), .width(5), .disabled(0), .enable("false")) multiplexer_6 (
    .in0(D_INSN_DEC_rt), .in1({5{1'b0}}), .in2(D_INSN_DEC_rd), .in3({5{1'b0}}), .in4(D_INSN_DEC_rd),
    .in5({5{1'b0}}), .in6(D_INSN_DEC_rd), .in7(D_INSN_DEC_rd), .in8(D_INSN_DEC_rd), .in9({5{1'b0}}),
    .in10({5{1'b0}}), .in11({5{1'b0}}), .in12({5{1'b0}}), .in13({5{1'b0}}), .in14({5{1'b0}}),
    .in15({5{1'b0}}), .in16({5{1'b0}}), .in17({5{1'b0}}), .in18({5{1'b0}}), .in19({5{1'b0}}),
    .in20({5{1'b0}}), .in21({5{1'b0}}), .in22(5'b11110), .in23({5{1'b0}}), .in24({5{1'b0}}),
    .in25({5{1'b0}}), .in26({5{1'b0}}), .in27({5{1'b0}}), .in28({5{1'b0}}), .in29({5{1'b0}}),
    .in30({5{1'b0}}), .in31({5{1'b0}}), .out(D_CTRL_RD), .sel(D_INSN_DEC_opcode));
  assign D_TARGET = {{5{1'b0}}, D_INSN_DEC_target};  // Bit_Extender bit_extender_2
  // Probe on W_RES_ID
  // Probe on M_RESOLVED_DATA
  eq5 eq5_8 (.in1(5'b10101), .in2(D_INSN_DEC_opcode), .out(D_SETX));
  eq5 eq5_9 (.in1(5'b00011), .in2(D_INSN_DEC_opcode), .out(D_JAL));
  eq5 eq5_10 (.in1(5'b01000), .in2(D_INSN_DEC_opcode), .out(D_LW));
  eq5 eq5_11 (.in1(5'b00111), .in2(D_INSN_DEC_opcode), .out(eq5_11_out));
  eq5 eq5_12 (.in1(5'b00101), .in2(D_INSN_DEC_opcode), .out(eq5_12_out));
  eq5 eq5_13 (.in1({5{1'b0}}), .in2(D_INSN_DEC_opcode), .out(eq5_13_out));
  register_resolver D_RESOLVE_RD (
    .reg_id(D_CTRL_RD), .in0_valid(1'b1), .in0_id(D_CTRL_RD), .in1_valid(M_RES_VALID), .in1_id(M_RES_ID),
    .in2_valid(X_RES_VALID), .in2_id(X_RES_ID), .in3_valid(1'b0), .in0_data(D_FILTERED_RD), .in1_data(M_RES),
    .in2_data(X_RES), .out_valid(D_RESOLVE_RD_out_valid), .out_data(D_RESOLVE_RD_out_data));  // open: in3_id, in3_data
  register_resolver D_RESOLVE_RS (
    .reg_id(D_CTRL_RS), .in0_valid(1'b1), .in0_id(D_CTRL_RS), .in1_valid(M_RES_VALID), .in1_id(M_RES_ID),
    .in2_valid(X_RES_VALID), .in2_id(X_RES_ID), .in3_valid(1'b0), .in0_data(D_FILTERED_RS), .in1_data(M_RES),
    .in2_data(X_RES), .out_valid(D_RESOLVE_RS_out_valid), .out_data(D_RESOLVE_RS_out_data));  // open: in3_id, in3_data
  // OR_Gate or_5 has open pins: in0=D_LW, in1=eq5_11_out, in2=eq5_12_out, in3=eq5_13_out, out=open
  RegisterFile REG_FILE (
    .WriteData(M_RESOLVED_DATA), .RegWriteEnable(W_RES_VALID), .clk(clk), .reset(reset),
    .ReadData2(D_RES_RD), .ReadReg2(D_CTRL_RD), .ReadData1(D_RES_RS), .WriteReg(W_RES_ID),
    .ReadReg1(D_CTRL_RS));
  nor nor_1 (nor_1_out, D_SETX, D_JAL);
  branch_resolver D_RESOLVE_CTRL (
    .insn(D_INSN), .pc(D_PC), .rd_no_conflicts(D_CTRL_RD_OK), .rd_valid(D_RESOLVE_RD_out_valid),
    .rd_data(D_RESOLVE_RD_out_data), .rs_valid(D_RESOLVE_RS_out_valid), .rs_data(D_RESOLVE_RS_out_data),
    .recovery(D_CTRL_RECOVERY), .next_pc(D_CTRL_NEXT_PC), .rs_no_conflicts(D_CTRL_RS_OK));
  // Probe on D_RES_RS
  // Probe on D_RES_RD
  pipeline_register X_CACHE_RD (
    .id_in(D_CTRL_RD), .valid_in(1'b1), .clk(clk), .reset(reset), .enable(1'b1), .id_out(X_CACHE_RD_id_out),
    .valid_out(X_CACHE_RD_valid_out), .data_out(X_CACHE_RD_data_out), .data_in(D_FILTERED_RD),
    .no_propagate(CLR_X));
  pipeline_register X_CACHE_RS (
    .id_in(D_CTRL_RS), .valid_in(1'b1), .clk(clk), .reset(reset), .enable(1'b1), .id_out(X_CACHE_RS_id_out),
    .valid_out(X_CACHE_RS_valid_out), .data_out(X_CACHE_RS_data_out), .data_in(D_FILTERED_RS),
    .no_propagate(CLR_X));
  writeback_selector writeback_selector_1 (
    .id_new(W_RES_ID), .valid_new(W_RES_VALID), .data_new(M_RESOLVED_DATA), .id_default(D_CTRL_RS),
    .valid_default(nor_1_out), .data_default(D_RES_RS), .data_out(writeback_selector_1_data_out));
  writeback_selector writeback_selector_2 (
    .id_new(W_RES_ID), .valid_new(W_RES_VALID), .data_new(M_RESOLVED_DATA), .id_default(D_CTRL_RD),
    .valid_default(nor_1_out), .data_default(D_RES_RD), .data_out(writeback_selector_2_data_out));
  register_resolver X_RESOLVE_RD (
    .reg_id(X_CTRL_RD), .in0_valid(X_CACHE_RD_valid_out), .in0_id(X_CACHE_RD_id_out),
    .in1_valid(M_RES_VALID), .in1_id(M_RES_ID), .in2_valid(1'b0), .in3_valid(1'b0),
    .in0_data(X_CACHE_RD_data_out), .in1_data(M_RES), .out_valid(X_RESOLVE_RD_out_valid),
    .out_data(X_RESOLVE_RD_out_data));  // open: in2_id, in3_id, in2_data, in3_data
  register_resolver X_RESOLVE_RS (
    .reg_id(X_CTRL_RS), .in0_valid(X_CACHE_RS_valid_out), .in0_id(X_CACHE_RS_id_out),
    .in1_valid(M_RES_VALID), .in1_id(M_RES_ID), .in2_valid(1'b0), .in3_valid(1'b0),
    .in0_data(X_CACHE_RS_data_out), .in1_data(M_RES), .out_valid(X_RESOLVE_RS_out_valid),
    .out_data(X_RESOLVE_RS_out_data));  // open: in2_id, in3_id, in2_data, in3_data
  writeback_selector writeback_selector_3 (
    .id_new(M_RES_ID), .valid_new(M_RES_VALID), .data_new(M_RES), .id_default(D_CTRL_RS),
    .valid_default(nor_1_out), .data_default(writeback_selector_1_data_out),
    .data_out(writeback_selector_3_data_out));
  writeback_selector writeback_selector_4 (
    .id_new(M_RES_ID), .valid_new(M_RES_VALID), .data_new(M_RES), .id_default(D_CTRL_RD),
    .valid_default(nor_1_out), .data_default(writeback_selector_2_data_out),
    .data_out(writeback_selector_4_data_out));
  writeback_selector writeback_selector_5 (
    .id_new(X_RES_ID), .valid_new(X_RES_VALID), .data_new(X_RES), .id_default(D_CTRL_RS),
    .valid_default(nor_1_out), .data_default(writeback_selector_3_data_out), .data_out(D_FILTERED_RS));
  writeback_selector writeback_selector_6 (
    .id_new(X_RES_ID), .valid_new(X_RES_VALID), .data_new(X_RES), .id_default(D_CTRL_RD),
    .valid_default(nor_1_out), .data_default(writeback_selector_4_data_out), .data_out(D_FILTERED_RD));
  branch_resolver branch_resolver_1 (
    .insn(X_INSN), .pc(X_PC), .rd_no_conflicts(M_CTRL_X_RD_OK), .rd_valid(X_RESOLVE_RD_out_valid),
    .rd_data(X_RESOLVE_RD_out_data), .rs_valid(X_RESOLVE_RS_out_valid), .rs_data(X_RESOLVE_RS_out_data),
    .recovery(CLR_X), .next_pc(X_CTRL_NEXT_PC), .rs_no_conflicts(M_CTRL_X_RS_OK));
  Priority_Encoder #(.select(2)) priority_encoder_1 (
    .in0(F_CTRL_RECOVERY), .in1(D_CTRL_RECOVERY), .in2(CLR_X), .out(priority_encoder_1_out),
    .gs(CTRL_RECOVERY), .en_in(1'b1));  // open: in3, en_out
  or or_6 (CLR_D, CLR_X, D_CTRL_RECOVERY);
  Multiplexer #(.width(32), .disabled(0), .enable("false")) multiplexer_7 (
    .in0(D_INSN), .in1({32{1'b0}}), .out(multiplexer_7_out), .sel(CLR_D));
  Multiplexer #(.select(2), .width(32), .disabled(0), .enable("false")) multiplexer_8 (
    .in0(F_CTRL_NEXT_PC), .in1(D_CTRL_NEXT_PC), .in2(X_CTRL_NEXT_PC), .out(CTRL_NEXT_PC),
    .sel(priority_encoder_1_out));  // open: in3
  or or_7 (CLR_F, CLR_D, F_CTRL_RECOVERY);
  Multiplexer #(.width(32), .disabled(0), .enable("false")) multiplexer_9 (
    .in0(D_FILTERED_RS), .in1(multiplexer_10_out), .out(multiplexer_9_out), .sel(or_8_out));
  Multiplexer #(.width(32), .disabled(0), .enable("false")) multiplexer_10 (
    .in0(D_PC), .in1(D_TARGET), .out(multiplexer_10_out), .sel(D_SETX));
  or or_8 (or_8_out, D_SETX, D_JAL);
  Multiplexer #(.width(32), .disabled(0), .enable("false")) multiplexer_11 (
    .in0(D_FILTERED_RD), .in1(multiplexer_12_out), .out(multiplexer_11_out), .sel(or_9_out));
  Multiplexer #(.width(32), .disabled(0), .enable("false")) multiplexer_12 (
    .in0(32'h1), .in1({32{1'b0}}), .out(multiplexer_12_out), .sel(D_SETX));
  or or_9 (or_9_out, D_SETX, D_JAL);
  register_32 u_X_INSN (.clk(clk), .\input (multiplexer_7_out), .enable(1'b1), .\output (X_INSN), .reset(reset));
  stage_resolution_checker X_CTRL_F_RD_CHECK (
    .insn(X_INSN), .\reg (F_CTRL_RD), .stage_has_resolved_arith(1'b1), .stage_has_resolved_lw(1'b0),
    .ok(X_CTRL_F_RD_OK));
  stage_resolution_checker X_CTRL_D_RD_CHECK (
    .insn(X_INSN), .\reg (D_CTRL_RD), .stage_has_resolved_arith(1'b1), .stage_has_resolved_lw(1'b0),
    .ok(X_CTRL_D_RD_OK));
  pipeline_register X_VAL1 (
    .id_in(D_CTRL_RS), .valid_in(nor_1_out), .clk(clk), .reset(reset), .enable(1'b1),
    .data_out(X_VAL1_data_out), .data_in(multiplexer_9_out), .no_propagate(CLR_X));  // open: id_out, valid_out
  pipeline_register X_VAL2 (
    .id_in(D_CTRL_RD), .valid_in(nor_1_out), .clk(clk), .reset(reset), .enable(1'b1), .id_out(X_VAL2_id_out),
    .valid_out(X_VAL2_valid_out), .data_out(X_VAL2_data_out), .data_in(multiplexer_11_out),
    .no_propagate(CLR_X));
  insn_decoder X_INSN_DEC (
    .insn(X_INSN), .aluop(X_INSN_DEC_aluop), .imm(X_INSN_DEC_imm), .opcode(X_INSN_DEC_opcode),
    .rd(X_CTRL_RD), .rs(X_CTRL_RS), .shamt(X_SHAMT));  // open: target, rt
  assign X_IMM = {{15{X_INSN_DEC_imm[16]}}, X_INSN_DEC_imm};  // Bit_Extender bit_extender_3
  // Probe on X_VAL1_data_out
  // Probe on multiplexer_13_out
  eq5 eq5_14 (.in1(5'b10101), .in2(X_INSN_DEC_opcode), .out(X_SETX));
  eq5 eq5_15 (.in1(5'b00011), .in2(X_INSN_DEC_opcode), .out(X_JAL));
  eq5 eq5_16 (.in1(5'b01000), .in2(X_INSN_DEC_opcode), .out(eq5_16_out));
  eq5 eq5_17 (.in1(5'b00111), .in2(X_INSN_DEC_opcode), .out(eq5_17_out));
  eq5 eq5_18 (.in1(5'b00101), .in2(X_INSN_DEC_opcode), .out(X_ADDI));
  eq5 eq5_19 (.in1(X_INSN_DEC_opcode), .in2({5{1'b0}}), .out(eq5_19_out));
  Multiplexer #(.width(32), .disabled(0), .enable("false")) multiplexer_13 (
    .in0(X_VAL2_data_out), .in1(X_IMM), .out(multiplexer_13_out), .sel(or_13_out));
  or or_10 (or_10_out, eq5_16_out, eq5_17_out);
  or or_11 (or_11_out, X_ADDI, eq5_19_out);
  Multiplexer #(.width(5), .disabled(0), .enable("false")) multiplexer_14 (
    .in0({5{1'b0}}), .in1(X_INSN_DEC_aluop), .out(X_ALUOP), .sel(eq5_19_out));
  stage_resolution_checker X_CTRL_F_RS_CHECK (
    .insn(X_INSN), .\reg (F_CTRL_RS), .stage_has_resolved_arith(1'b1), .stage_has_resolved_lw(1'b0),
    .ok(X_CTRL_F_RS_OK));
  stage_resolution_checker X_CTRL_D_RS_CHECK (
    .insn(X_INSN), .\reg (D_CTRL_RS), .stage_has_resolved_arith(1'b1), .stage_has_resolved_lw(1'b0),
    .ok(X_CTRL_D_RS_OK));
  ALU alu_1 (
    .InputData1(X_VAL1_data_out), .ALUop(X_ALUOP), .InputData2(multiplexer_13_out), .out_7(alu_1_out_7),
    .shift(X_SHAMT), .ovf(alu_1_ovf));  // open: BLT, BNE
  or or_12 (or_12_out, X_SETX, X_JAL);
  Multiplexer #(.width(5), .disabled(0), .enable("false")) multiplexer_15 (
    .in0(X_CTRL_RD), .in1(X_CTRL_RS), .out(multiplexer_15_out), .sel(or_10_out));
  or or_13 (or_13_out, or_10_out, X_ADDI);
  or or_14 (X_RES_VALID, or_12_out, or_11_out);
  eq5 eq5_20 (.in1({5{1'b0}}), .in2(X_INSN_DEC_aluop), .out(eq5_20_out));
  eq5 eq5_21 (.in1(5'b00001), .in2(X_INSN_DEC_aluop), .out(eq5_21_out));
  eq5 eq5_22 (.in1(5'b00111), .in2(X_INSN_DEC_aluop), .out(X_ALUOP_HDEC));
  Multiplexer #(.width(5), .disabled(0), .enable("false")) multiplexer_16 (
    .in0(multiplexer_15_out), .in1({5{1'b1}}), .out(multiplexer_16_out), .sel(X_JAL));
  // Probe on alu_1_out_7
  or or_15 (or_15_out, eq5_20_out, eq5_21_out, X_ALUOP_HDEC);
  and and_2 (and_2_out, alu_1_ovf, or_11_out, X_GEN_EXC);
  or or_16 (X_GEN_EXC, or_15_out, X_ADDI);
  Multiplexer #(.width(5), .disabled(0), .enable("false")) multiplexer_17 (
    .in0(multiplexer_16_out), .in1(5'b11110), .out(X_RES_ID), .sel(or_17_out));
  or or_17 (or_17_out, X_SETX, and_2_out);
  Multiplexer #(.width(32), .disabled(0), .enable("false")) multiplexer_18 (
    .in0(multiplexer_19_out), .in1(32'h4), .out(multiplexer_18_out), .sel(X_ALUOP_HDEC));
  Multiplexer #(.select(2), .width(32), .disabled(0), .enable("false")) multiplexer_19 (
    .in0(32'h1), .in1(32'h2), .in2(32'h3), .in3(32'h3), .out(multiplexer_19_out), .sel({X_ADDI, X_ALUOP[0]}));
  Multiplexer #(.width(32), .disabled(0), .enable("false")) multiplexer_20 (
    .in0(X_INSN), .in1({32{1'b0}}), .out(multiplexer_20_out), .sel(CLR_X));
  Multiplexer #(.width(32), .disabled(0), .enable("false")) multiplexer_21 (
    .in0(alu_1_out_7), .in1(multiplexer_18_out), .out(X_RES), .sel(and_2_out));
  register_32 u_M_INSN (.clk(clk), .\input (multiplexer_20_out), .enable(1'b1), .\output (M_INSN), .reset(reset));
  pipeline_register M_VAL1 (
    .id_in(X_RES_ID), .valid_in(X_RES_VALID), .clk(clk), .reset(reset), .enable(1'b1),
    .id_out(M_VAL1_id_out), .valid_out(M_VAL1_valid_out), .data_out(M_VAL1_data_out), .data_in(X_RES),
    .no_propagate(1'b0));
  pipeline_register M_VAL2 (
    .id_in(X_VAL2_id_out), .valid_in(X_VAL2_valid_out), .clk(clk), .reset(reset), .enable(1'b1),
    .id_out(M_VAL2_id_out), .valid_out(M_VAL2_valid_out), .data_out(M_VAL2_data_out),
    .data_in(X_VAL2_data_out), .no_propagate(1'b0));
  insn_decoder M_INSN_DEC (
    .insn(M_INSN), .imm(M_IMM), .opcode(M_INSN_DEC_opcode), .rd(M_RD));  // open: aluop, target, rs, rt, shamt
  stage_resolution_checker M_CTRL_F_RD_CHECK (
    .insn(M_INSN), .\reg (F_CTRL_RD), .stage_has_resolved_arith(1'b1), .stage_has_resolved_lw(1'b1),
    .ok(M_CTRL_F_RD_OK));
  stage_resolution_checker M_CTRL_D_RD_CHECK (
    .insn(M_INSN), .\reg (D_CTRL_RD), .stage_has_resolved_arith(1'b1), .stage_has_resolved_lw(1'b1),
    .ok(M_CTRL_D_RD_OK));
  stage_resolution_checker M_CTRL_X_RD_CHECK (
    .insn(M_INSN), .\reg (X_CTRL_RD), .stage_has_resolved_arith(1'b1), .stage_has_resolved_lw(1'b1),
    .ok(M_CTRL_X_RD_OK));
  writeback_selector writeback_selector_7 (
    .id_new(W_RES_ID), .valid_new(W_RES_VALID), .data_new(M_RESOLVED_ADDR), .id_default(M_VAL1_id_out),
    .valid_default(1'b1), .data_default(M_VAL1_data_out), .data_out(writeback_selector_7_data_out));
  writeback_selector writeback_selector_8 (
    .id_new(W_RES_ID), .valid_new(W_RES_VALID), .data_new(M_RESOLVED_DATA), .id_default(M_VAL2_id_out),
    .valid_default(M_VAL2_valid_out), .data_default(M_VAL2_data_out), .data_out(writeback_selector_8_data_out));
  eq5 eq5_23 (.in1(5'b00111), .in2(M_INSN_DEC_opcode), .out(M_SW));
  eq5 eq5_24 (.in1(M_INSN_DEC_opcode), .in2(5'b01000), .out(M_LW));
  Multiplexer #(.width(32), .disabled(0), .enable("false")) multiplexer_22 (
    .in0(M_VAL1_data_out), .in1(writeback_selector_7_data_out), .out(multiplexer_22_out), .sel(M_RESOLVE));
  Multiplexer #(.width(32), .disabled(0), .enable("false")) multiplexer_23 (
    .in0(M_VAL2_data_out), .in1(writeback_selector_8_data_out), .out(multiplexer_23_out), .sel(M_RESOLVE));
  stage_resolution_checker M_CTRL_F_RS_CHECK (
    .insn(M_INSN), .\reg (F_CTRL_RS), .stage_has_resolved_arith(1'b1), .stage_has_resolved_lw(1'b1),
    .ok(M_CTRL_F_RS_OK));
  stage_resolution_checker M_CTRL_D_RS_CHECK (
    .insn(M_INSN), .\reg (D_CTRL_RS), .stage_has_resolved_arith(1'b1), .stage_has_resolved_lw(1'b1),
    .ok(M_CTRL_D_RS_OK));
  stage_resolution_checker M_CTRL_X_RS_CHECK (
    .insn(M_INSN), .\reg (X_CTRL_RS), .stage_has_resolved_arith(1'b1), .stage_has_resolved_lw(1'b1),
    .ok(M_CTRL_X_RS_OK));
  // Probe on multiplexer_22_out
  // Probe on multiplexer_23_out
  or or_18 (M_RES_VALID, M_VAL1_valid_out, M_LW);
  // Probe on M_VAL1_data_out
  Bit_Extender #(.in_width(32), .out_width(12)) bit_extender_4 (.in(multiplexer_22_out), .out(bit_extender_4_out));
  Multiplexer #(.width(5), .disabled(0), .enable("false")) multiplexer_24 (
    .in0(M_VAL1_id_out), .in1(M_RD), .out(M_RES_ID), .sel(M_LW));
  RAM #(.addrWidth(12), .dataWidth(32), .bus("separate")) ram_1 (
    .addr(bit_extender_4_out), .din(multiplexer_23_out), .data(ram_1_data), .str(M_SW), .sel(1'b1),
    .clk(not_1_out), .ld(1'b1));  // open: clr
  not not_1 (not_1_out, clk);
  Multiplexer #(.width(32), .disabled(0), .enable("false")) multiplexer_25 (
    .in0(M_VAL1_data_out), .in1(ram_1_data), .out(M_RES), .sel(M_LW));
  // Probe on ram_1_data
  register_32 u_W_INSN (.clk(clk), .\input (M_INSN), .enable(1'b1), .\output (W_INSN), .reset(reset));
  pipeline_register M_VAL1_2 (
    .id_in(M_RES_ID), .valid_in(M_RES_VALID), .clk(clk), .reset(reset), .enable(1'b1), .id_out(W_RES_ID),
    .valid_out(W_RES_VALID), .data_out(M_RESOLVED_DATA), .data_in(M_RES), .no_propagate(1'b0));
  insn_decoder W_INSN_DEC (.insn(W_INSN), .opcode(W_INSN_DEC_opcode));  // open: aluop, target, imm, rd, rs, rt, shamt
  stage_resolution_checker W_CTRL_F_RD_CHECK (
    .insn(W_INSN), .\reg (F_CTRL_RD), .stage_has_resolved_arith(1'b1), .stage_has_resolved_lw(1'b1),
    .ok(W_CTRL_F_RD_CHECK_ok));
  stage_resolution_checker W_CTRL_F_RS_CHECK (
    .insn(W_INSN), .\reg (F_CTRL_RS), .stage_has_resolved_arith(1'b1), .stage_has_resolved_lw(1'b1),
    .ok(W_CTRL_F_RS_CHECK_ok));
  assign bit_extender_5_out = {{15{1'b0}}, M_IMM};  // Bit_Extender bit_extender_5
  eq5 eq5_25 (.in1(W_INSN_DEC_opcode), .in2(5'b01000), .out(M_RESOLVE));
  _32_bit_compact u_32_bit_compact_2 (
    .result(M_RESOLVED_ADDR), .A(M_RESOLVED_DATA), .B(bit_extender_5_out), .sub(1'b0));  // open: ovf
  and and_3 (F_CTRL_RD_OK, W_CTRL_F_RD_CHECK_ok, M_CTRL_F_RD_OK, X_CTRL_F_RD_OK, D_CTRL_F_RD_OK);
  and and_4 (D_CTRL_RD_OK, M_CTRL_D_RD_OK, X_CTRL_D_RD_OK);
  and and_5 (F_CTRL_RS_OK, W_CTRL_F_RS_CHECK_ok, M_CTRL_F_RS_OK, X_CTRL_F_RS_OK, D_CTRL_F_RS_OK);
  and and_6 (D_CTRL_RS_OK, M_CTRL_D_RS_OK, X_CTRL_D_RS_OK);

  // Other names for the same wires on the sheet: W_RES[31:0] = M_RESOLVED_DATA; X_CTRL_RD_OK = M_CTRL_X_RD_OK;
  //   X_CTRL_RECOVERY = CLR_X; X_CTRL_RS_OK = M_CTRL_X_RS_OK; X_RD[4:0] = X_CTRL_RD; X_RS[4:0] = X_CTRL_RS

  // Notes on the sheet:
  //   contents of rom_1 (hex, n*v repeats v):
  //   2f400fff 8000092 2a400000 2944000 2ac00001 2d60d10 2ad7ffff 20c0690 18c8020 20c0894 18c8020 20c0290
  //   18c8020 30cb008 3b140000 2a520001 2a940001 324bfff5 27c00000 3ffa0000 3c3bffff 3c7bfffe 3cbbfffd
  //   2f7bfffc 2c0a0000 39200000 38200001 2c200002 2c4000cc 4620c10 2c800088 4a40c10 8000030 b000002b
  //   12480004 39e00000 3ca00001 2c200002 27c00000 39e00000 3a600001 2c200002 27c00000 a8000000 39e00000
  //   3c600001 2c200002 27c00000 29c00001 1ce0e10 2fc00036 2080018 250001c 8000021 2ac00002 2d60e10
  //   2b000001 2b400001 2fc00040 1d6d00c 2080018 210c020 250001c 8000021 3180090 2b5a0001 1301fff8
  //   2ac00003 2d60e10 2b000101 2b400001 2b800012 2fc0004e 1d6d00c 2080018 210c020 250001c 8000021 3180090
  //   2b5a0001 335dfff8 2ac00004 2d60e10 2b400008 2b800010 2fc0005d 31ae000 1d6c00c 3180d10 2080018
  //   210c020 250001c 8000021 35a0094 1341fff7 39c0094 35c0094 1341fff4 2ac00005 2d60e10 2b400001 35a0c90
  //   2b800019 2bc00010 2fc00072 31e0810 1d6c00c 1cee00c 3180510 318d00c 2080018 210c020 250001c 8000021
  //   35a0194 2b9dfffd 1341fff4 2b400001 35a0c90 2b800019 3de0094 13c1ffef 2ac00006 2d60e10 2b400001
  //   35a0f10 2b80001f 2bc00001 3de0f90 2fc00088 1d6e00c 31af00c 2080018 210c020 250001c 8000021 35a0094
  //   2b9dffff 1341fff7 28a00000 2f7a0004 47fa0000 443bffff 447bfffe 44bbfffd 27c00000 2d000008 29000000
  //   29680000 29800028 18000002 2d400000 29680008 412a0000 18000013 29440008 2d6a0001 3569fffb
  //   There is a hazard if sw/lw immediately follows lw
endmodule

module RegisterFile (
  input  [31:0] WriteData,
  input  RegWriteEnable,
  input  clk,
  input  reset,
  input  [4:0] ReadReg2,
  input  [4:0] WriteReg,
  input  [4:0] ReadReg1,
  output [31:0] ReadData2,
  output [31:0] ReadData1
);

  wire decoder_1_out0, decoder_1_out1, decoder_1_out2, decoder_1_out3, decoder_1_out4, decoder_1_out5,
       decoder_1_out6, decoder_1_out7, decoder_1_out8, decoder_1_out9, decoder_1_out10, decoder_1_out11,
       decoder_1_out12, decoder_1_out13, decoder_1_out14, decoder_1_out15, decoder_1_out16, decoder_1_out17,
       decoder_1_out18, decoder_1_out19, decoder_1_out20, decoder_1_out21, decoder_1_out22, decoder_1_out23,
       decoder_1_out24, decoder_1_out25, decoder_1_out26, decoder_1_out27, decoder_1_out28, decoder_1_out29,
       decoder_1_out30, decoder_1_out31, decoder_2_out0, decoder_2_out1, decoder_2_out2, decoder_2_out3,
       decoder_2_out4, decoder_2_out5, decoder_2_out6, decoder_2_out7, decoder_2_out8, decoder_2_out9,
       decoder_2_out10, decoder_2_out11, decoder_2_out12, decoder_2_out13, decoder_2_out14, decoder_2_out15,
       decoder_2_out16, decoder_2_out17, decoder_2_out18, decoder_2_out19, decoder_2_out20, decoder_2_out21,
       decoder_2_out22, decoder_2_out23, decoder_2_out24, decoder_2_out25, decoder_2_out26, decoder_2_out27,
       decoder_2_out28, decoder_2_out29, decoder_2_out30, decoder_2_out31, en0, en1, en2, en3, en4, en5, en6,
       en7, en8, en9, en10, en11, en12, en13, en14, en15, en16, en17, en18, en19, en20, en21, en22, en23,
       en24, en25, en26, en27, en28, en29, en30, en31;
  wire [4:0] multiplexer_1_out;
  wire [31:0] _0, _1, _2, _3, _4, _5, _6, _7, _8, _9, _10, _11, _12, _13, _14, _15, _16, _17, _18, _19, _20,
       _21, _22, _23, _24, _25, _26, _27, _28, _29, _30, _31;

  assign ReadData2 = decoder_1_out0 ? _0 : 32'bz;  // Controlled_Buffer controlled_buffer_1
  assign ReadData1 = decoder_2_out0 ? _0 : 32'bz;  // Controlled_Buffer controlled_buffer_2
  assign ReadData2 = decoder_1_out1 ? _1 : 32'bz;  // Controlled_Buffer controlled_buffer_3
  assign ReadData1 = decoder_2_out1 ? _1 : 32'bz;  // Controlled_Buffer controlled_buffer_4
  register_32 register_32_1 (.clk(clk), .\input (WriteData), .enable(1'b0), .\output (_0), .reset(reset));
  register_32 register_32_2 (.clk(clk), .\input (WriteData), .enable(en1), .\output (_1), .reset(reset));
  register_32 register_32_3 (.clk(clk), .\input (WriteData), .enable(en2), .\output (_2), .reset(reset));
  register_32 register_32_4 (.clk(clk), .\input (WriteData), .enable(en3), .\output (_3), .reset(reset));
  register_32 register_32_5 (.clk(clk), .\input (WriteData), .enable(en4), .\output (_4), .reset(reset));
  register_32 register_32_6 (.clk(clk), .\input (WriteData), .enable(en5), .\output (_5), .reset(reset));
  register_32 register_32_7 (.clk(clk), .\input (WriteData), .enable(en6), .\output (_6), .reset(reset));
  register_32 register_32_8 (.clk(clk), .\input (WriteData), .enable(en7), .\output (_7), .reset(reset));
  assign ReadData2 = decoder_1_out3 ? _3 : 32'bz;  // Controlled_Buffer controlled_buffer_5
  assign ReadData2 = decoder_1_out2 ? _2 : 32'bz;  // Controlled_Buffer controlled_buffer_6
  assign ReadData1 = decoder_2_out2 ? _2 : 32'bz;  // Controlled_Buffer controlled_buffer_7
  assign ReadData1 = decoder_2_out3 ? _3 : 32'bz;  // Controlled_Buffer controlled_buffer_8
  assign ReadData2 = decoder_1_out4 ? _4 : 32'bz;  // Controlled_Buffer controlled_buffer_9
  assign ReadData1 = decoder_2_out4 ? _4 : 32'bz;  // Controlled_Buffer controlled_buffer_10
  assign ReadData1 = decoder_2_out5 ? _5 : 32'bz;  // Controlled_Buffer controlled_buffer_11
  assign ReadData2 = decoder_1_out6 ? _6 : 32'bz;  // Controlled_Buffer controlled_buffer_12
  assign ReadData2 = decoder_1_out5 ? _5 : 32'bz;  // Controlled_Buffer controlled_buffer_13
  assign ReadData1 = decoder_2_out6 ? _6 : 32'bz;  // Controlled_Buffer controlled_buffer_14
  register_32 register_32_9 (.clk(clk), .\input (WriteData), .enable(en8), .\output (_8), .reset(reset));
  register_32 register_32_10 (.clk(clk), .\input (WriteData), .enable(en9), .\output (_9), .reset(reset));
  register_32 register_32_11 (.clk(clk), .\input (WriteData), .enable(en10), .\output (_10), .reset(reset));
  register_32 register_32_12 (.clk(clk), .\input (WriteData), .enable(en11), .\output (_11), .reset(reset));
  register_32 register_32_13 (.clk(clk), .\input (WriteData), .enable(en12), .\output (_12), .reset(reset));
  register_32 register_32_14 (.clk(clk), .\input (WriteData), .enable(en13), .\output (_13), .reset(reset));
  register_32 register_32_15 (.clk(clk), .\input (WriteData), .enable(en14), .\output (_14), .reset(reset));
  register_32 register_32_16 (.clk(clk), .\input (WriteData), .enable(en15), .\output (_15), .reset(reset));
  assign ReadData2 = decoder_1_out8 ? _8 : 32'bz;  // Controlled_Buffer controlled_buffer_15
  assign ReadData2 = decoder_1_out7 ? _7 : 32'bz;  // Controlled_Buffer controlled_buffer_16
  assign ReadData1 = decoder_2_out7 ? _7 : 32'bz;  // Controlled_Buffer controlled_buffer_17
  assign ReadData1 = decoder_2_out8 ? _8 : 32'bz;  // Controlled_Buffer controlled_buffer_18
  assign ReadData2 = decoder_1_out9 ? _9 : 32'bz;  // Controlled_Buffer controlled_buffer_19
  assign ReadData1 = decoder_2_out9 ? _9 : 32'bz;  // Controlled_Buffer controlled_buffer_20
  assign ReadData2 = decoder_1_out11 ? _11 : 32'bz;  // Controlled_Buffer controlled_buffer_21
  assign ReadData2 = decoder_1_out10 ? _10 : 32'bz;  // Controlled_Buffer controlled_buffer_22
  assign ReadData1 = decoder_2_out11 ? _11 : 32'bz;  // Controlled_Buffer controlled_buffer_23
  assign ReadData1 = decoder_2_out10 ? _10 : 32'bz;  // Controlled_Buffer controlled_buffer_24
  assign ReadData2 = decoder_1_out12 ? _12 : 32'bz;  // Controlled_Buffer controlled_buffer_25
  assign ReadData1 = decoder_2_out12 ? _12 : 32'bz;  // Controlled_Buffer controlled_buffer_26
  assign ReadData1 = decoder_2_out13 ? _13 : 32'bz;  // Controlled_Buffer controlled_buffer_27
  register_32 register_32_17 (.clk(clk), .\input (WriteData), .enable(en16), .\output (_16), .reset(reset));
  register_32 register_32_18 (.clk(clk), .\input (WriteData), .enable(en17), .\output (_17), .reset(reset));
  register_32 register_32_19 (.clk(clk), .\input (WriteData), .enable(en18), .\output (_18), .reset(reset));
  register_32 register_32_20 (.clk(clk), .\input (WriteData), .enable(en19), .\output (_19), .reset(reset));
  register_32 register_32_21 (.clk(clk), .\input (WriteData), .enable(en20), .\output (_20), .reset(reset));
  register_32 register_32_22 (.clk(clk), .\input (WriteData), .enable(en21), .\output (_21), .reset(reset));
  register_32 register_32_23 (.clk(clk), .\input (WriteData), .enable(en22), .\output (_22), .reset(reset));
  register_32 register_32_24 (.clk(clk), .\input (WriteData), .enable(en23), .\output (_23), .reset(reset));
  assign ReadData2 = decoder_1_out14 ? _14 : 32'bz;  // Controlled_Buffer controlled_buffer_28
  assign ReadData2 = decoder_1_out13 ? _13 : 32'bz;  // Controlled_Buffer controlled_buffer_29
  Decoder #(.select(5), .enable("false")) decoder_1 (
    .out0(decoder_1_out0), .out1(decoder_1_out1), .out2(decoder_1_out2), .out3(decoder_1_out3),
    .out4(decoder_1_out4), .out5(decoder_1_out5), .out6(decoder_1_out6), .out7(decoder_1_out7),
    .out8(decoder_1_out8), .out9(decoder_1_out9), .out10(decoder_1_out10), .out11(decoder_1_out11),
    .out12(decoder_1_out12), .out13(decoder_1_out13), .out14(decoder_1_out14), .out15(decoder_1_out15),
    .out16(decoder_1_out16), .out17(decoder_1_out17), .out18(decoder_1_out18), .out19(decoder_1_out19),
    .out20(decoder_1_out20), .out21(decoder_1_out21), .out22(decoder_1_out22), .out23(decoder_1_out23),
    .out24(decoder_1_out24), .out25(decoder_1_out25), .out26(decoder_1_out26), .out27(decoder_1_out27),
    .out28(decoder_1_out28), .out29(decoder_1_out29), .out30(decoder_1_out30), .out31(decoder_1_out31),
    .sel(ReadReg2));
  assign ReadData1 = decoder_2_out14 ? _14 : 32'bz;  // Controlled_Buffer controlled_buffer_30
  Decoder #(.select(5), .enable("false")) decoder_2 (
    .out0(decoder_2_out0), .out1(decoder_2_out1), .out2(decoder_2_out2), .out3(decoder_2_out3),
    .out4(decoder_2_out4), .out5(decoder_2_out5), .out6(decoder_2_out6), .out7(decoder_2_out7),
    .out8(decoder_2_out8), .out9(decoder_2_out9), .out10(decoder_2_out10), .out11(decoder_2_out11),
    .out12(decoder_2_out12), .out13(decoder_2_out13), .out14(decoder_2_out14), .out15(decoder_2_out15),
    .out16(decoder_2_out16), .out17(decoder_2_out17), .out18(decoder_2_out18), .out19(decoder_2_out19),
    .out20(decoder_2_out20), .out21(decoder_2_out21), .out22(decoder_2_out22), .out23(decoder_2_out23),
    .out24(decoder_2_out24), .out25(decoder_2_out25), .out26(decoder_2_out26), .out27(decoder_2_out27),
    .out28(decoder_2_out28), .out29(decoder_2_out29), .out30(decoder_2_out30), .out31(decoder_2_out31),
    .sel(ReadReg1));
  assign ReadData2 = decoder_1_out15 ? _15 : 32'bz;  // Controlled_Buffer controlled_buffer_31
  assign ReadData1 = decoder_2_out15 ? _15 : 32'bz;  // Controlled_Buffer controlled_buffer_32
  assign ReadData2 = decoder_1_out16 ? _16 : 32'bz;  // Controlled_Buffer controlled_buffer_33
  assign ReadData1 = decoder_2_out16 ? _16 : 32'bz;  // Controlled_Buffer controlled_buffer_34
  register_32 register_32_25 (.clk(clk), .\input (WriteData), .enable(en24), .\output (_24), .reset(reset));
  register_32 register_32_26 (.clk(clk), .\input (WriteData), .enable(en25), .\output (_25), .reset(reset));
  register_32 register_32_27 (.clk(clk), .\input (WriteData), .enable(en26), .\output (_26), .reset(reset));
  register_32 register_32_28 (.clk(clk), .\input (WriteData), .enable(en27), .\output (_27), .reset(reset));
  register_32 register_32_29 (.clk(clk), .\input (WriteData), .enable(en28), .\output (_28), .reset(reset));
  register_32 register_32_30 (.clk(clk), .\input (WriteData), .enable(en29), .\output (_29), .reset(reset));
  register_32 register_32_31 (.clk(clk), .\input (WriteData), .enable(en30), .\output (_30), .reset(reset));
  register_32 register_32_32 (.clk(clk), .\input (WriteData), .enable(en31), .\output (_31), .reset(reset));
  assign ReadData2 = decoder_1_out18 ? _18 : 32'bz;  // Controlled_Buffer controlled_buffer_35
  assign ReadData2 = decoder_1_out17 ? _17 : 32'bz;  // Controlled_Buffer controlled_buffer_36
  assign ReadData1 = decoder_2_out17 ? _17 : 32'bz;  // Controlled_Buffer controlled_buffer_37
  assign ReadData1 = decoder_2_out18 ? _18 : 32'bz;  // Controlled_Buffer controlled_buffer_38
  assign ReadData2 = decoder_1_out19 ? _19 : 32'bz;  // Controlled_Buffer controlled_buffer_39
  assign ReadData1 = decoder_2_out19 ? _19 : 32'bz;  // Controlled_Buffer controlled_buffer_40
  assign ReadData1 = decoder_2_out20 ? _20 : 32'bz;  // Controlled_Buffer controlled_buffer_41
  assign ReadData2 = decoder_1_out20 ? _20 : 32'bz;  // Controlled_Buffer controlled_buffer_42
  assign ReadData2 = decoder_1_out21 ? _21 : 32'bz;  // Controlled_Buffer controlled_buffer_43
  assign ReadData1 = decoder_2_out21 ? _21 : 32'bz;  // Controlled_Buffer controlled_buffer_44
  assign ReadData2 = decoder_1_out23 ? _23 : 32'bz;  // Controlled_Buffer controlled_buffer_45
  assign ReadData2 = decoder_1_out22 ? _22 : 32'bz;  // Controlled_Buffer controlled_buffer_46
  assign ReadData1 = decoder_2_out23 ? _23 : 32'bz;  // Controlled_Buffer controlled_buffer_47
  assign ReadData1 = decoder_2_out22 ? _22 : 32'bz;  // Controlled_Buffer controlled_buffer_48
  assign ReadData2 = decoder_1_out24 ? _24 : 32'bz;  // Controlled_Buffer controlled_buffer_49
  assign ReadData1 = decoder_2_out24 ? _24 : 32'bz;  // Controlled_Buffer controlled_buffer_50
  // Probe on _0
  // Probe on _1
  // Probe on _2
  // Probe on _3
  // Probe on _4
  // Probe on _5
  // Probe on _6
  // Probe on _7
  assign ReadData2 = decoder_1_out26 ? _26 : 32'bz;  // Controlled_Buffer controlled_buffer_51
  assign ReadData2 = decoder_1_out25 ? _25 : 32'bz;  // Controlled_Buffer controlled_buffer_52
  assign ReadData1 = decoder_2_out26 ? _26 : 32'bz;  // Controlled_Buffer controlled_buffer_53
  assign ReadData1 = decoder_2_out25 ? _25 : 32'bz;  // Controlled_Buffer controlled_buffer_54
  assign ReadData2 = decoder_1_out27 ? _27 : 32'bz;  // Controlled_Buffer controlled_buffer_55
  assign ReadData1 = decoder_2_out28 ? _28 : 32'bz;  // Controlled_Buffer controlled_buffer_56
  assign ReadData1 = decoder_2_out27 ? _27 : 32'bz;  // Controlled_Buffer controlled_buffer_57
  assign ReadData2 = decoder_1_out28 ? _28 : 32'bz;  // Controlled_Buffer controlled_buffer_58
  assign ReadData2 = decoder_1_out29 ? _29 : 32'bz;  // Controlled_Buffer controlled_buffer_59
  assign ReadData1 = decoder_2_out29 ? _29 : 32'bz;  // Controlled_Buffer controlled_buffer_60
  // Probe on _8
  // Probe on _9
  // Probe on _10
  // Probe on _11
  // Probe on _12
  // Probe on _13
  // Probe on _14
  // Probe on _15
  assign ReadData2 = decoder_1_out31 ? _31 : 32'bz;  // Controlled_Buffer controlled_buffer_61
  assign ReadData2 = decoder_1_out30 ? _30 : 32'bz;  // Controlled_Buffer controlled_buffer_62
  assign ReadData1 = decoder_2_out31 ? _31 : 32'bz;  // Controlled_Buffer controlled_buffer_63
  assign ReadData1 = decoder_2_out30 ? _30 : 32'bz;  // Controlled_Buffer controlled_buffer_64
  // Probe on _16
  // Probe on _17
  // Probe on _18
  // Probe on _19
  // Probe on _20
  // Probe on _21
  // Probe on _22
  // Probe on _23
  // Probe on _24
  // Probe on _25
  // Probe on _26
  // Probe on _27
  // Probe on _28
  // Probe on _29
  // Probe on _30
  // Probe on _31
  Multiplexer #(.width(5), .enable("false")) multiplexer_1 (
    .in0({5{1'b0}}), .in1(WriteReg), .out(multiplexer_1_out), .sel(RegWriteEnable));
  Decoder #(.select(5), .enable("false")) decoder_3 (
    .out0(en0), .out1(en1), .out2(en2), .out3(en3), .out4(en4), .out5(en5), .out6(en6), .out7(en7),
    .out8(en8), .out9(en9), .out10(en10), .out11(en11), .out12(en12), .out13(en13), .out14(en14),
    .out15(en15), .out16(en16), .out17(en17), .out18(en18), .out19(en19), .out20(en20), .out21(en21),
    .out22(en22), .out23(en23), .out24(en24), .out25(en25), .out26(en26), .out27(en27), .out28(en28),
    .out29(en29), .out30(en30), .out31(en31), .sel(multiplexer_1_out));

  // Other names for the same wires on the sheet: data[31:0] = WriteData; enab = RegWriteEnable
endmodule

module register_32 (
  input  enable,
  input  reset,
  input  clk,
  input  [31:0] \input ,
  output [31:0] \output 
);

  wire enable_t, not_1_out;

  not not_1 (not_1_out, clk);
  and and_1 (enable_t, not_1_out, enable);
  D_Flip_Flop d_ff_1 (.clk(clk), .D(\input [0]), .Q(\output [0]), .en(enable_t), .reset(reset));  // open: Qn, preset
  D_Flip_Flop d_ff_2 (.clk(clk), .D(\input [1]), .Q(\output [1]), .en(enable_t), .reset(reset));  // open: Qn, preset
  D_Flip_Flop d_ff_3 (.clk(clk), .D(\input [2]), .Q(\output [2]), .en(enable_t), .reset(reset));  // open: Qn, preset
  D_Flip_Flop d_ff_4 (.clk(clk), .D(\input [3]), .Q(\output [3]), .en(enable_t), .reset(reset));  // open: Qn, preset
  D_Flip_Flop d_ff_5 (.clk(clk), .D(\input [4]), .Q(\output [4]), .en(enable_t), .reset(reset));  // open: Qn, preset
  D_Flip_Flop d_ff_6 (.clk(clk), .D(\input [5]), .Q(\output [5]), .en(enable_t), .reset(reset));  // open: Qn, preset
  D_Flip_Flop d_ff_7 (.clk(clk), .D(\input [6]), .Q(\output [6]), .en(enable_t), .reset(reset));  // open: Qn, preset
  D_Flip_Flop d_ff_8 (.clk(clk), .D(\input [7]), .Q(\output [7]), .en(enable_t), .reset(reset));  // open: Qn, preset
  D_Flip_Flop d_ff_9 (.clk(clk), .D(\input [16]), .Q(\output [16]), .en(enable_t), .reset(reset));  // open: Qn, preset
  D_Flip_Flop d_ff_10 (.clk(clk), .D(\input [17]), .Q(\output [17]), .en(enable_t), .reset(reset));  // open: Qn, preset
  D_Flip_Flop d_ff_11 (.clk(clk), .D(\input [18]), .Q(\output [18]), .en(enable_t), .reset(reset));  // open: Qn, preset
  D_Flip_Flop d_ff_12 (.clk(clk), .D(\input [19]), .Q(\output [19]), .en(enable_t), .reset(reset));  // open: Qn, preset
  D_Flip_Flop d_ff_13 (.clk(clk), .D(\input [20]), .Q(\output [20]), .en(enable_t), .reset(reset));  // open: Qn, preset
  D_Flip_Flop d_ff_14 (.clk(clk), .D(\input [21]), .Q(\output [21]), .en(enable_t), .reset(reset));  // open: Qn, preset
  D_Flip_Flop d_ff_15 (.clk(clk), .D(\input [22]), .Q(\output [22]), .en(enable_t), .reset(reset));  // open: Qn, preset
  D_Flip_Flop d_ff_16 (.clk(clk), .D(\input [23]), .Q(\output [23]), .en(enable_t), .reset(reset));  // open: Qn, preset
  D_Flip_Flop d_ff_17 (.clk(clk), .D(\input [8]), .Q(\output [8]), .en(enable_t), .reset(reset));  // open: Qn, preset
  D_Flip_Flop d_ff_18 (.clk(clk), .D(\input [9]), .Q(\output [9]), .en(enable_t), .reset(reset));  // open: Qn, preset
  D_Flip_Flop d_ff_19 (.clk(clk), .D(\input [10]), .Q(\output [10]), .en(enable_t), .reset(reset));  // open: Qn, preset
  D_Flip_Flop d_ff_20 (.clk(clk), .D(\input [11]), .Q(\output [11]), .en(enable_t), .reset(reset));  // open: Qn, preset
  D_Flip_Flop d_ff_21 (.clk(clk), .D(\input [12]), .Q(\output [12]), .en(enable_t), .reset(reset));  // open: Qn, preset
  D_Flip_Flop d_ff_22 (.clk(clk), .D(\input [13]), .Q(\output [13]), .en(enable_t), .reset(reset));  // open: Qn, preset
  D_Flip_Flop d_ff_23 (.clk(clk), .D(\input [14]), .Q(\output [14]), .en(enable_t), .reset(reset));  // open: Qn, preset
  D_Flip_Flop d_ff_24 (.clk(clk), .D(\input [15]), .Q(\output [15]), .en(enable_t), .reset(reset));  // open: Qn, preset
  D_Flip_Flop d_ff_25 (.clk(clk), .D(\input [24]), .Q(\output [24]), .en(enable_t), .reset(reset));  // open: Qn, preset
  D_Flip_Flop d_ff_26 (.clk(clk), .D(\input [25]), .Q(\output [25]), .en(enable_t), .reset(reset));  // open: Qn, preset
  D_Flip_Flop d_ff_27 (.clk(clk), .D(\input [26]), .Q(\output [26]), .en(enable_t), .reset(reset));  // open: Qn, preset
  D_Flip_Flop d_ff_28 (.clk(clk), .D(\input [27]), .Q(\output [27]), .en(enable_t), .reset(reset));  // open: Qn, preset
  D_Flip_Flop d_ff_29 (.clk(clk), .D(\input [28]), .Q(\output [28]), .en(enable_t), .reset(reset));  // open: Qn, preset
  D_Flip_Flop d_ff_30 (.clk(clk), .D(\input [29]), .Q(\output [29]), .en(enable_t), .reset(reset));  // open: Qn, preset
  D_Flip_Flop d_ff_31 (.clk(clk), .D(\input [30]), .Q(\output [30]), .en(enable_t), .reset(reset));  // open: Qn, preset
  D_Flip_Flop d_ff_32 (.clk(clk), .D(\input [31]), .Q(\output [31]), .en(enable_t), .reset(reset));  // open: Qn, preset

  // Other names for the same wires on the sheet: first[7:0] = \input [7:0]; second[7:0] = \input [15:8];
  //   third[7:0] = \input [23:16]; fourth[7:0] = \input [31:24]
endmodule

module ALU (
  input  [4:0] shift,
  input  [31:0] InputData1,
  input  [31:0] InputData2,
  input  [4:0] ALUop,
  output BNE,
  output BLT,
  output [31:0] out_7,
  output ovf
);

  wire comparator_1_eq, hamming_decoder_1_error, n32_bit_compact_1_ovf, n32_bit_compact_2_ovf;
  wire [4:0] hamming_encoder_1_parity;
  wire [5:0] bitadder_1_out;
  wire [25:0] hamming_decoder_1_data_out;
  wire [31:0] and_1_out, bit_extender_1_out, bit_extender_2_out, n32_bit_compact_1_result,
       n32_bit_compact_2_result, not_1_out, or_1_out, shifter_1_out, shifter_2_out, xor_1_out;
  wire [31:31] hamming_encoder_1_security;

  Shifter #(.width(32)) shifter_1 (.in(InputData1), .\dist (shift), .out(shifter_1_out));
  Shifter #(.width(32), .shift("ar")) shifter_2 (.in(InputData1), .\dist (shift), .out(shifter_2_out));
  _32_bit_compact u_32_bit_compact_1 (
    .result(n32_bit_compact_1_result), .A(InputData1), .B(InputData2), .ovf(n32_bit_compact_1_ovf), .sub(1'b0));
  _32_bit_compact u_32_bit_compact_2 (
    .result(n32_bit_compact_2_result), .A(InputData1), .B(InputData2), .ovf(n32_bit_compact_2_ovf), .sub(1'b1));
  assign and_1_out = InputData1 & InputData2;  // AND_Gate and_1, 32 bits wide
  assign or_1_out = InputData1 | InputData2;  // OR_Gate or_1, 32 bits wide
  assign xor_1_out = InputData1 ^ InputData2;  // XOR_Gate xor_1, 32 bits wide
  assign not_1_out = ~InputData1;  // NOT_Gate not_1, 32 bits wide
  hamming_encoder hamming_encoder_1 (
    .data_input(InputData1[25:0]), .security(hamming_encoder_1_security[31]),
    .parity(hamming_encoder_1_parity));
  hamming_decoder hamming_decoder_1 (
    .data_in(InputData1), .data_out(hamming_decoder_1_data_out), .error(hamming_decoder_1_error));
  BitAdder #(.width(32)) bitadder_1 (.in0(InputData1), .out(bitadder_1_out));
  assign bit_extender_1_out = {{6{1'b0}}, hamming_decoder_1_data_out};  // Bit_Extender bit_extender_1
  assign bit_extender_2_out = {{26{1'b0}}, bitadder_1_out};  // Bit_Extender bit_extender_2
  Multiplexer #(.select(5), .width(32), .enable("false")) multiplexer_1 (
    .in0(n32_bit_compact_1_result), .in1(n32_bit_compact_2_result), .in2(and_1_out), .in3(or_1_out),
    .in4(shifter_1_out), .in5(shifter_2_out),
    .in6({hamming_encoder_1_security[31], hamming_encoder_1_parity, InputData1[25:0]}),
    .in7(bit_extender_1_out), .in8(xor_1_out), .in9(not_1_out), .in10(bit_extender_2_out), .out(out_7),
    .sel(ALUop));  // open: in11, in12, in13, in14, in15, in16, in17, in18, in19, in20, in21, in22, in23, in24, in25, in26, in27, in28, in29, in30, in31
  Multiplexer #(.select(5), .enable("false")) multiplexer_2 (
    .in0(n32_bit_compact_1_ovf), .in1(n32_bit_compact_2_ovf), .in2(1'b0), .in3(1'b0), .in4(1'b0), .in5(1'b0),
    .in6(1'b0), .in7(hamming_decoder_1_error), .in8(1'b0), .in9(1'b0), .in10(1'b0), .in11(1'b0), .in12(1'b0),
    .in13(1'b0), .in14(1'b0), .in15(1'b0), .in16(1'b0), .in17(1'b0), .in18(1'b0), .in19(1'b0), .in20(1'b0),
    .in21(1'b0), .in22(1'b0), .in23(1'b0), .in24(1'b0), .in25(1'b0), .in26(1'b0), .in27(1'b0), .in28(1'b0),
    .in29(1'b0), .in30(1'b0), .in31(1'b0), .out(ovf), .sel(ALUop));
  Comparator #(.width(32)) comparator_1 (.a(InputData1), .b(InputData2), .eq(comparator_1_eq), .lt(BLT));  // open: gt
  not not_2 (BNE, comparator_1_eq);

  // Other names for the same wires on the sheet: A[31:0] = InputData1; B[31:0] = InputData2
endmodule

module one_bit_add (
  input  cin,
  input  a,
  input  b,
  output cout,
  output sum
);

  wire and_1_out, and_2_out, xor_1_out;

  or or_1 (cout, and_1_out, and_2_out);
  xor xor_1 (xor_1_out, a, b);
  and and_1 (and_1_out, a, b);
  and and_2 (and_2_out, xor_1_out, cin);
  xor xor_2 (sum, cin, xor_1_out);
endmodule

module _32_bit_add (
  input  a31,
  input  b31,
  input  a30,
  input  b30,
  input  a29,
  input  b29,
  input  a28,
  input  b28,
  input  a27,
  input  b27,
  input  a26,
  input  b26,
  input  a25,
  input  b25,
  input  a24,
  input  b24,
  input  a23,
  input  b23,
  input  a22,
  input  b22,
  input  a21,
  input  b21,
  input  a20,
  input  b20,
  input  a19,
  input  b19,
  input  a18,
  input  b18,
  input  a17,
  input  b17,
  input  a16,
  input  b16,
  input  add_sub,
  input  a15,
  input  b15,
  input  a14,
  input  b14,
  input  a13,
  input  b13,
  input  a12,
  input  b12,
  input  a11,
  input  b11,
  input  a10,
  input  b10,
  input  a9,
  input  b9,
  input  a8,
  input  b8,
  input  a7,
  input  b7,
  input  a6,
  input  b6,
  input  a5,
  input  b5,
  input  a4,
  input  b4,
  input  a3,
  input  b3,
  input  a2,
  input  b2,
  input  a1,
  input  b1,
  input  a0,
  input  b0,
  output ovf,
  output s31,
  output s30,
  output s29,
  output s28,
  output s27,
  output s26,
  output s25,
  output s24,
  output cout,
  output s23,
  output s22,
  output s21,
  output s20,
  output s19,
  output s18,
  output s17,
  output s16,
  output s15,
  output s14,
  output s13,
  output s12,
  output s11,
  output s10,
  output s9,
  output s8,
  output s7,
  output s6,
  output s5,
  output s4,
  output s3,
  output s2,
  output s1,
  output s0
);

  wire one_bit_add_2_cout, one_bit_add_3_cout, one_bit_add_4_cout, one_bit_add_5_cout, one_bit_add_6_cout,
       one_bit_add_7_cout, one_bit_add_8_cout, one_bit_add_9_cout, one_bit_add_10_cout, one_bit_add_11_cout,
       one_bit_add_12_cout, one_bit_add_13_cout, one_bit_add_14_cout, one_bit_add_15_cout,
       one_bit_add_16_cout, one_bit_add_17_cout, one_bit_add_18_cout, one_bit_add_19_cout,
       one_bit_add_20_cout, one_bit_add_21_cout, one_bit_add_22_cout, one_bit_add_23_cout,
       one_bit_add_24_cout, one_bit_add_25_cout, one_bit_add_26_cout, one_bit_add_27_cout,
       one_bit_add_28_cout, one_bit_add_29_cout, one_bit_add_30_cout, one_bit_add_31_cout,
       one_bit_add_32_cout, xor_2_out, xor_3_out, xor_4_out, xor_5_out, xor_6_out, xor_7_out, xor_8_out,
       xor_9_out, xor_10_out, xor_11_out, xor_12_out, xor_13_out, xor_14_out, xor_15_out, xor_16_out,
       xor_17_out, xor_18_out, xor_19_out, xor_20_out, xor_21_out, xor_22_out, xor_23_out, xor_24_out,
       xor_25_out, xor_26_out, xor_27_out, xor_28_out, xor_29_out, xor_30_out, xor_31_out, xor_32_out,
       xor_33_out;

  xor xor_1 (ovf, cout, one_bit_add_5_cout);
  one_bit_add one_bit_add_1 (.a(a31), .b(xor_2_out), .cout(cout), .cin(one_bit_add_5_cout), .sum(s31));
  xor xor_2 (xor_2_out, add_sub, b31);
  one_bit_add one_bit_add_2 (.a(a23), .b(xor_3_out), .cout(one_bit_add_2_cout), .cin(one_bit_add_6_cout), .sum(s23));
  xor xor_3 (xor_3_out, add_sub, b23);
  one_bit_add one_bit_add_3 (.a(a15), .b(xor_4_out), .cout(one_bit_add_3_cout), .cin(one_bit_add_7_cout), .sum(s15));
  xor xor_4 (xor_4_out, add_sub, b15);
  one_bit_add one_bit_add_4 (.a(a7), .b(xor_5_out), .cout(one_bit_add_4_cout), .cin(one_bit_add_8_cout), .sum(s7));
  xor xor_5 (xor_5_out, add_sub, b7);
  one_bit_add one_bit_add_5 (.a(a30), .b(xor_6_out), .cout(one_bit_add_5_cout), .cin(one_bit_add_9_cout), .sum(s30));
  xor xor_6 (xor_6_out, add_sub, b30);
  one_bit_add one_bit_add_6 (.a(a22), .b(xor_7_out), .cout(one_bit_add_6_cout), .cin(one_bit_add_10_cout), .sum(s22));
  xor xor_7 (xor_7_out, add_sub, b22);
  one_bit_add one_bit_add_7 (.a(a14), .b(xor_8_out), .cout(one_bit_add_7_cout), .cin(one_bit_add_11_cout), .sum(s14));
  xor xor_8 (xor_8_out, add_sub, b14);
  one_bit_add one_bit_add_8 (.a(a6), .b(xor_9_out), .cout(one_bit_add_8_cout), .cin(one_bit_add_12_cout), .sum(s6));
  xor xor_9 (xor_9_out, add_sub, b6);
  one_bit_add one_bit_add_9 (.a(a29), .b(xor_10_out), .cout(one_bit_add_9_cout), .cin(one_bit_add_13_cout), .sum(s29));
  xor xor_10 (xor_10_out, add_sub, b29);
  one_bit_add one_bit_add_10 (
    .a(a21), .b(xor_11_out), .cout(one_bit_add_10_cout), .cin(one_bit_add_14_cout), .sum(s21));
  xor xor_11 (xor_11_out, add_sub, b21);
  one_bit_add one_bit_add_11 (
    .a(a13), .b(xor_12_out), .cout(one_bit_add_11_cout), .cin(one_bit_add_15_cout), .sum(s13));
  xor xor_12 (xor_12_out, add_sub, b13);
  one_bit_add one_bit_add_12 (.a(a5), .b(xor_13_out), .cout(one_bit_add_12_cout), .cin(one_bit_add_16_cout), .sum(s5));
  xor xor_13 (xor_13_out, add_sub, b5);
  one_bit_add one_bit_add_13 (
    .a(a28), .b(xor_14_out), .cout(one_bit_add_13_cout), .cin(one_bit_add_17_cout), .sum(s28));
  xor xor_14 (xor_14_out, add_sub, b28);
  one_bit_add one_bit_add_14 (
    .a(a20), .b(xor_15_out), .cout(one_bit_add_14_cout), .cin(one_bit_add_18_cout), .sum(s20));
  xor xor_15 (xor_15_out, add_sub, b20);
  one_bit_add one_bit_add_15 (
    .a(a12), .b(xor_16_out), .cout(one_bit_add_15_cout), .cin(one_bit_add_19_cout), .sum(s12));
  xor xor_16 (xor_16_out, add_sub, b12);
  one_bit_add one_bit_add_16 (.a(a4), .b(xor_17_out), .cout(one_bit_add_16_cout), .cin(one_bit_add_20_cout), .sum(s4));
  one_bit_add one_bit_add_17 (
    .a(a27), .b(xor_18_out), .cout(one_bit_add_17_cout), .cin(one_bit_add_21_cout), .sum(s27));
  one_bit_add one_bit_add_18 (
    .a(a19), .b(xor_19_out), .cout(one_bit_add_18_cout), .cin(one_bit_add_22_cout), .sum(s19));
  one_bit_add one_bit_add_19 (
    .a(a11), .b(xor_20_out), .cout(one_bit_add_19_cout), .cin(one_bit_add_23_cout), .sum(s11));
  one_bit_add one_bit_add_20 (.a(a3), .b(xor_21_out), .cout(one_bit_add_20_cout), .cin(one_bit_add_25_cout), .sum(s3));
  xor xor_17 (xor_17_out, add_sub, b4);
  one_bit_add one_bit_add_21 (
    .a(a26), .b(xor_22_out), .cout(one_bit_add_21_cout), .cin(one_bit_add_24_cout), .sum(s26));
  xor xor_18 (xor_18_out, add_sub, b27);
  one_bit_add one_bit_add_22 (
    .a(a18), .b(xor_23_out), .cout(one_bit_add_22_cout), .cin(one_bit_add_26_cout), .sum(s18));
  xor xor_19 (xor_19_out, add_sub, b19);
  one_bit_add one_bit_add_23 (
    .a(a10), .b(xor_24_out), .cout(one_bit_add_23_cout), .cin(one_bit_add_27_cout), .sum(s10));
  xor xor_20 (xor_20_out, add_sub, b11);
  xor xor_21 (xor_21_out, add_sub, b3);
  one_bit_add one_bit_add_24 (
    .a(a25), .b(xor_26_out), .cout(one_bit_add_24_cout), .cin(one_bit_add_29_cout), .sum(s25));
  xor xor_22 (xor_22_out, add_sub, b26);
  xor xor_23 (xor_23_out, add_sub, b18);
  xor xor_24 (xor_24_out, add_sub, b10);
  one_bit_add one_bit_add_25 (.a(a2), .b(xor_25_out), .cout(one_bit_add_25_cout), .cin(one_bit_add_28_cout), .sum(s2));
  xor xor_25 (xor_25_out, add_sub, b2);
  xor xor_26 (xor_26_out, add_sub, b25);
  one_bit_add one_bit_add_26 (
    .a(a17), .b(xor_27_out), .cout(one_bit_add_26_cout), .cin(one_bit_add_30_cout), .sum(s17));
  xor xor_27 (xor_27_out, add_sub, b17);
  one_bit_add one_bit_add_27 (.a(a9), .b(xor_28_out), .cout(one_bit_add_27_cout), .cin(one_bit_add_31_cout), .sum(s9));
  xor xor_28 (xor_28_out, add_sub, b9);
  one_bit_add one_bit_add_28 (.a(a1), .b(xor_29_out), .cout(one_bit_add_28_cout), .cin(one_bit_add_32_cout), .sum(s1));
  xor xor_29 (xor_29_out, add_sub, b1);
  one_bit_add one_bit_add_29 (.a(a24), .b(xor_30_out), .cout(one_bit_add_29_cout), .cin(one_bit_add_2_cout), .sum(s24));
  xor xor_30 (xor_30_out, add_sub, b24);
  one_bit_add one_bit_add_30 (.a(a16), .b(xor_31_out), .cout(one_bit_add_30_cout), .cin(one_bit_add_3_cout), .sum(s16));
  xor xor_31 (xor_31_out, add_sub, b16);
  one_bit_add one_bit_add_31 (.a(a8), .b(xor_32_out), .cout(one_bit_add_31_cout), .cin(one_bit_add_4_cout), .sum(s8));
  xor xor_32 (xor_32_out, add_sub, b8);
  one_bit_add one_bit_add_32 (.a(a0), .b(xor_33_out), .cout(one_bit_add_32_cout), .cin(add_sub), .sum(s0));
  xor xor_33 (xor_33_out, add_sub, b0);
endmodule

module _32_bit_compact (
  input  [31:0] A,
  input  [31:0] B,
  input  sub,
  output ovf,
  output [31:0] result
);

  _32_bit_add u_32_bit_add_1 (
    .add_sub(sub), .ovf(ovf), .s7(result[7]), .s31(result[31]), .s23(result[23]), .s15(result[15]),
    .s30(result[30]), .s22(result[22]), .s14(result[14]), .s6(result[6]), .s29(result[29]), .s21(result[21]),
    .s13(result[13]), .s5(result[5]), .s28(result[28]), .s20(result[20]), .s12(result[12]), .s4(result[4]),
    .s27(result[27]), .s19(result[19]), .s11(result[11]), .s3(result[3]), .s26(result[26]), .s18(result[18]),
    .s10(result[10]), .s2(result[2]), .s25(result[25]), .s17(result[17]), .s9(result[9]), .s1(result[1]),
    .s24(result[24]), .s16(result[16]), .s8(result[8]), .s0(result[0]), .a31(A[31]), .a23(A[23]),
    .a15(A[15]), .a7(A[7]), .b31(B[31]), .b23(B[23]), .b15(B[15]), .b7(B[7]), .a30(A[30]), .a22(A[22]),
    .a14(A[14]), .a6(A[6]), .b30(B[30]), .b22(B[22]), .b14(B[14]), .b6(B[6]), .a29(A[29]), .a21(A[21]),
    .a13(A[13]), .a5(A[5]), .b29(B[29]), .b21(B[21]), .b13(B[13]), .b5(B[5]), .a28(A[28]), .a20(A[20]),
    .a12(A[12]), .a4(A[4]), .b28(B[28]), .b20(B[20]), .b12(B[12]), .b4(B[4]), .a27(A[27]), .a19(A[19]),
    .a11(A[11]), .a3(A[3]), .b27(B[27]), .b19(B[19]), .b11(B[11]), .b3(B[3]), .a26(A[26]), .a18(A[18]),
    .a10(A[10]), .a2(A[2]), .b26(B[26]), .b18(B[18]), .b10(B[10]), .b2(B[2]), .a25(A[25]), .a17(A[17]),
    .a9(A[9]), .a1(A[1]), .b25(B[25]), .b17(B[17]), .b9(B[9]), .b1(B[1]), .a24(A[24]), .a16(A[16]),
    .a8(A[8]), .a0(A[0]), .b24(B[24]), .b16(B[16]), .b8(B[8]), .b0(B[0]));  // open: cout
endmodule

module insn_decoder (
  input  [31:0] insn,
  output [16:0] imm,
  output [4:0] aluop,
  output [26:0] target,
  output [4:0] shamt,
  output [4:0] rt,
  output [4:0] rs,
  output [4:0] rd,
  output [4:0] opcode
);


  assign aluop = insn[6:2];
  assign imm = insn[16:0];
  assign opcode = insn[31:27];
  assign rd = insn[26:22];
  assign rs = insn[21:17];
  assign rt = insn[16:12];
  assign shamt = insn[11:7];
  assign target = insn[26:0];
endmodule

module pipeline_register (
  input  [4:0] id_in,
  input  no_propagate,
  input  valid_in,
  input  [31:0] data_in,
  input  clk,
  input  reset,
  input  enable,
  output [4:0] id_out,
  output valid_out,
  output [31:0] data_out
);

  wire and_1_out, eq5_1_out, multiplexer_2_out;
  wire [4:0] multiplexer_1_out;
  wire [31:0] multiplexer_3_out, register_32_1_output;

  Multiplexer #(.width(5), .disabled(0), .enable("false")) multiplexer_1 (
    .in0(id_in), .in1({5{1'b0}}), .out(multiplexer_1_out), .sel(no_propagate));
  Multiplexer #(.disabled(0), .enable("false")) multiplexer_2 (
    .in0(valid_in), .in1(1'b0), .out(multiplexer_2_out), .sel(no_propagate));
  Multiplexer #(.width(32), .disabled(0), .enable("false")) multiplexer_3 (
    .in0(data_in), .in1({32{1'b0}}), .out(multiplexer_3_out), .sel(no_propagate));
  D_Flip_Flop d_ff_1 (
    .clk(clk), .D(multiplexer_1_out[0]), .Q(id_out[0]), .en(enable), .reset(reset));  // open: Qn, preset
  D_Flip_Flop d_ff_2 (
    .clk(clk), .D(multiplexer_1_out[1]), .Q(id_out[1]), .en(enable), .reset(reset));  // open: Qn, preset
  D_Flip_Flop d_ff_3 (
    .clk(clk), .D(multiplexer_1_out[2]), .Q(id_out[2]), .en(enable), .reset(reset));  // open: Qn, preset
  D_Flip_Flop d_ff_4 (
    .clk(clk), .D(multiplexer_1_out[3]), .Q(id_out[3]), .en(enable), .reset(reset));  // open: Qn, preset
  D_Flip_Flop d_ff_5 (
    .clk(clk), .D(multiplexer_1_out[4]), .Q(id_out[4]), .en(enable), .reset(reset));  // open: Qn, preset
  D_Flip_Flop d_ff_6 (.clk(clk), .D(multiplexer_2_out), .Q(valid_out), .en(enable), .reset(reset));  // open: Qn, preset
  register_32 register_32_1 (
    .clk(clk), .\input (multiplexer_3_out), .enable(enable), .\output (register_32_1_output), .reset(reset));
  eq5 eq5_1 (.in1(id_out), .in2({5{1'b0}}), .out(eq5_1_out));
  and and_1 (and_1_out, eq5_1_out, valid_out);
  Multiplexer #(.width(32), .disabled(0), .enable("false")) multiplexer_4 (
    .in0(register_32_1_output), .in1({32{1'b0}}), .out(data_out), .sel(and_1_out));

  // Notes on the sheet:
  //   Enforce requirement that $r0 = 0
endmodule

module writeback_selector (
  input  [4:0] id_new,
  input  valid_new,
  input  [31:0] data_new,
  input  [4:0] id_default,
  input  valid_default,
  input  [31:0] data_default,
  output [31:0] data_out
);

  wire and_1_out, and_2_out, and_3_out, and_4_out, eq5_1_out, eq5_2_out, not_1_out;
  wire [31:0] multiplexer_1_out, multiplexer_2_out;

  and and_1 (and_1_out, valid_new, valid_default);
  eq5 eq5_1 (.in1(id_new), .in2(id_default), .out(eq5_1_out));
  eq5 eq5_2 (.in1(id_default), .in2({5{1'b0}}), .out(eq5_2_out));
  and and_2 (and_2_out, eq5_1_out, and_1_out);
  Multiplexer #(.width(32), .disabled(0), .enable("false")) multiplexer_1 (
    .in0(data_default), .in1(data_new), .out(multiplexer_1_out), .sel(and_2_out));
  and and_3 (and_3_out, eq5_2_out, valid_default);
  not not_1 (not_1_out, valid_default);
  Multiplexer #(.width(32), .disabled(0), .enable("false")) multiplexer_2 (
    .in0(multiplexer_1_out), .in1({32{1'b0}}), .out(multiplexer_2_out), .sel(and_3_out));
  and and_4 (and_4_out, not_1_out, valid_new, eq5_1_out);
  Multiplexer #(.width(32), .disabled(0), .enable("false")) multiplexer_3 (
    .in0(multiplexer_2_out), .in1(data_new), .out(data_out), .sel(and_4_out));
endmodule

module stage_resolution_checker (
  input  [31:0] insn,
  input  [4:0] \reg ,
  input  stage_has_resolved_arith,
  input  stage_has_resolved_lw,
  output ok
);

  wire and_1_out, and_2_out, and_3_out, and_5_out, eq5_1_out, eq5_2_out, eq5_3_out, eq5_4_out, eq5_6_out,
       eq5_7_out, eq5_8_out, eq5_9_out, eq5_10_out, INSN_ARITH, INSN_LW, not_1_out, not_2_out, or_1_out,
       or_2_out, or_3_out, or_5_out, POSSIBLE_EXC, VALID_OP;
  wire [4:0] insn_decoder_1_aluop, insn_decoder_1_opcode, insn_decoder_1_rd, multiplexer_1_out,
       multiplexer_2_out;

  insn_decoder insn_decoder_1 (
    .insn(insn), .aluop(insn_decoder_1_aluop), .opcode(insn_decoder_1_opcode), .rd(insn_decoder_1_rd));  // open: target, imm, rs, rt, shamt
  eq5 eq5_1 (.in1({5{1'b0}}), .in2(insn_decoder_1_aluop), .out(eq5_1_out));
  eq5 eq5_2 (.in1(insn_decoder_1_aluop), .in2(5'b00001), .out(eq5_2_out));
  eq5 eq5_3 (.in1(insn_decoder_1_aluop), .in2(5'b00111), .out(eq5_3_out));
  eq5 eq5_4 (.in1({5{1'b0}}), .in2(insn_decoder_1_opcode), .out(eq5_4_out));
  or or_1 (or_1_out, eq5_1_out, eq5_2_out, eq5_3_out);
  eq5 eq5_5 (.in1(5'b01000), .in2(insn_decoder_1_opcode), .out(INSN_LW));
  eq5 eq5_6 (.in1(5'b10101), .in2(insn_decoder_1_opcode), .out(eq5_6_out));
  eq5 eq5_7 (.in1(5'b00011), .in2(insn_decoder_1_opcode), .out(eq5_7_out));
  eq5 eq5_8 (.in1(5'b00101), .in2(insn_decoder_1_opcode), .out(eq5_8_out));
  and and_1 (and_1_out, stage_has_resolved_arith, INSN_ARITH);
  and and_2 (and_2_out, stage_has_resolved_lw, INSN_LW);
  or or_2 (or_2_out, INSN_LW, INSN_ARITH);
  not not_1 (not_1_out, or_2_out);
  and and_3 (and_3_out, eq5_4_out, or_1_out);
  eq5 eq5_9 (.in1(5'b11110), .in2(\reg ), .out(eq5_9_out));
  or or_3 (or_3_out, and_1_out, and_2_out, not_1_out);
  or or_4 (INSN_ARITH, eq5_6_out, eq5_7_out, eq5_8_out, eq5_4_out);
  or or_5 (or_5_out, eq5_8_out, and_3_out);
  Multiplexer #(.width(5), .disabled(0), .enable("false")) multiplexer_1 (
    .in0(insn_decoder_1_rd), .in1({5{1'b1}}), .out(multiplexer_1_out), .sel(eq5_7_out));
  Multiplexer #(.width(5), .disabled(0), .enable("false")) multiplexer_2 (
    .in0(multiplexer_1_out), .in1(5'b11110), .out(multiplexer_2_out), .sel(eq5_6_out));
  and and_4 (POSSIBLE_EXC, or_5_out, eq5_9_out);
  eq5 eq5_10 (.in1(multiplexer_2_out), .in2(\reg ), .out(eq5_10_out));
  or or_6 (VALID_OP, POSSIBLE_EXC, eq5_10_out);
  not not_2 (not_2_out, VALID_OP);
  and and_5 (and_5_out, VALID_OP, or_3_out);
  or or_7 (ok, not_2_out, and_5_out);
endmodule

module register_resolver (
  input  [4:0] reg_id,
  input  in0_valid,
  input  [4:0] in0_id,
  input  in1_valid,
  input  [4:0] in1_id,
  input  in2_valid,
  input  [4:0] in2_id,
  input  in3_valid,
  input  [4:0] in3_id,
  input  [31:0] in0_data,
  input  [31:0] in1_data,
  input  [31:0] in2_data,
  input  [31:0] in3_data,
  output out_valid,
  output [31:0] out_data
);

  wire and_1_out, and_2_out, and_3_out, and_4_out, eq5_1_out, eq5_2_out, eq5_3_out, eq5_4_out;
  wire [1:0] priority_encoder_1_out;

  eq5 eq5_1 (.in1(in0_id), .in2(reg_id), .out(eq5_1_out));
  eq5 eq5_2 (.in1(in1_id), .in2(reg_id), .out(eq5_2_out));
  eq5 eq5_3 (.in1(in2_id), .in2(reg_id), .out(eq5_3_out));
  eq5 eq5_4 (.in1(in3_id), .in2(reg_id), .out(eq5_4_out));
  and and_1 (and_1_out, in0_valid, eq5_1_out);
  and and_2 (and_2_out, in1_valid, eq5_2_out);
  and and_3 (and_3_out, in2_valid, eq5_3_out);
  and and_4 (and_4_out, in3_valid, eq5_4_out);
  Priority_Encoder #(.select(2)) priority_encoder_1 (
    .in0(and_1_out), .in1(and_2_out), .in2(and_3_out), .in3(and_4_out), .out(priority_encoder_1_out),
    .gs(out_valid));  // open: en_out, en_in
  Multiplexer #(.select(2), .width(32), .disabled(0)) multiplexer_1 (
    .in0(in0_data), .in1(in1_data), .in2(in2_data), .in3(in3_data), .out(out_data),
    .sel(priority_encoder_1_out), .en(out_valid));
endmodule

module branch_resolver (
  input  [31:0] insn,
  input  [31:0] pc,
  input  rd_no_conflicts,
  input  rd_valid,
  input  [31:0] rd_data,
  input  rs_no_conflicts,
  input  rs_valid,
  input  [31:0] rs_data,
  output recovery,
  output [31:0] next_pc
);

  wire and_1_out, and_2_out, and_3_out, and_4_out, and_5_out, and_6_out, and_7_out, cmp32_1_eq, cmp32_2_eq,
       cmp32_2_lt, eq5_1_out, eq5_2_out, eq5_3_out, eq5_4_out, not_1_out, not_2_out, or_1_out;
  wire [4:0] insn_decoder_1_opcode;
  wire [16:0] insn_decoder_1_imm;
  wire [26:0] insn_decoder_1_target;
  wire [31:0] IMM, multiplexer_1_out, multiplexer_2_out, n32_bit_compact_1_result, n32_bit_compact_2_result,
       TARGET;

  insn_decoder insn_decoder_1 (
    .insn(insn), .target(insn_decoder_1_target), .imm(insn_decoder_1_imm), .opcode(insn_decoder_1_opcode));  // open: aluop, rd, rs, rt, shamt
  assign IMM = {{15{insn_decoder_1_imm[16]}}, insn_decoder_1_imm};  // Bit_Extender bit_extender_1
  assign TARGET = {{5{1'b0}}, insn_decoder_1_target};  // Bit_Extender bit_extender_2
  and and_1 (and_1_out, rd_no_conflicts, rd_valid);
  cmp32 cmp32_1 (.in1({32{1'b0}}), .in2(rd_data), .eq(cmp32_1_eq));  // open: lt
  cmp32 cmp32_2 (.in1(rd_data), .in2(rs_data), .eq(cmp32_2_eq), .lt(cmp32_2_lt));
  and and_2 (and_2_out, rs_no_conflicts, rs_valid);
  eq5 eq5_1 (.in1(5'b00010), .in2(insn_decoder_1_opcode), .out(eq5_1_out));
  eq5 eq5_2 (.in1(5'b00110), .in2(insn_decoder_1_opcode), .out(eq5_2_out));
  eq5 eq5_3 (.in1(5'b10110), .in2(insn_decoder_1_opcode), .out(eq5_3_out));
  eq5 eq5_4 (.in1(5'b00100), .in2(insn_decoder_1_opcode), .out(eq5_4_out));
  not not_1 (not_1_out, cmp32_1_eq);
  not not_2 (not_2_out, cmp32_2_eq);
  and and_3 (and_3_out, and_1_out, and_2_out);
  and and_4 (and_4_out, eq5_1_out, and_3_out, not_2_out);
  and and_5 (and_5_out, eq5_2_out, and_3_out, cmp32_2_lt);
  and and_6 (and_6_out, eq5_3_out, not_1_out, and_1_out);
  and and_7 (and_7_out, eq5_4_out, and_1_out);
  Multiplexer #(.width(32), .disabled(0), .enable("false")) multiplexer_1 (
    .in0(pc), .in1(rd_data), .out(multiplexer_1_out), .sel(and_7_out));
  _32_bit_compact u_32_bit_compact_1 (.result(n32_bit_compact_1_result), .A(pc), .B(IMM), .sub(1'b0));  // open: ovf
  or or_1 (or_1_out, and_4_out, and_5_out);
  Multiplexer #(.width(32), .disabled(0), .enable("false")) multiplexer_2 (
    .in0(multiplexer_1_out), .in1(TARGET), .out(multiplexer_2_out), .sel(and_6_out));
  Multiplexer #(.width(32), .disabled(0), .enable("false")) multiplexer_3 (
    .in0(multiplexer_2_out), .in1(n32_bit_compact_2_result), .out(next_pc), .sel(or_1_out));
  _32_bit_compact u_32_bit_compact_2 (
    .result(n32_bit_compact_2_result), .A(32'h1), .B(n32_bit_compact_1_result), .sub(1'b0));  // open: ovf
  or or_2 (recovery, and_7_out, and_6_out, or_1_out);
endmodule

// EQ
module eq5 (
  input  [4:0] in1,
  input  [4:0] in2,
  output out
);

  wire xnor_1_out, xnor_2_out, xnor_3_out, xnor_4_out, xnor_5_out;

  xnor xnor_1 (xnor_1_out, in1[0], in2[0]);
  xnor xnor_2 (xnor_2_out, in1[1], in2[1]);
  xnor xnor_3 (xnor_3_out, in1[2], in2[2]);
  xnor xnor_4 (xnor_4_out, in1[3], in2[3]);
  xnor xnor_5 (xnor_5_out, in1[4], in2[4]);
  and and_1 (out, xnor_1_out, xnor_2_out, xnor_3_out, xnor_4_out, xnor_5_out);
endmodule

module cmp32 (
  input  [31:0] in1,
  input  [31:0] in2,
  output eq,
  output lt
);

  wire n32_bit_compact_1_ovf, nor_1_out, nor_2_out, nor_3_out, nor_4_out;
  wire [31:0] n32_bit_compact_1_result;

  _32_bit_compact u_32_bit_compact_1 (
    .result(n32_bit_compact_1_result), .A(in1), .B(in2), .ovf(n32_bit_compact_1_ovf), .sub(1'b1));
  nor nor_1 (nor_1_out, n32_bit_compact_1_result[0], n32_bit_compact_1_result[1], n32_bit_compact_1_result[2], n32_bit_compact_1_result[3], n32_bit_compact_1_result[4], n32_bit_compact_1_result[5], n32_bit_compact_1_result[6], n32_bit_compact_1_result[7]);
  xor xor_1 (lt, n32_bit_compact_1_result[31], n32_bit_compact_1_ovf);
  nor nor_2 (nor_2_out, n32_bit_compact_1_result[8], n32_bit_compact_1_result[9], n32_bit_compact_1_result[10], n32_bit_compact_1_result[11], n32_bit_compact_1_result[12], n32_bit_compact_1_result[13], n32_bit_compact_1_result[14], n32_bit_compact_1_result[15]);
  nor nor_3 (nor_3_out, n32_bit_compact_1_result[16], n32_bit_compact_1_result[17], n32_bit_compact_1_result[18], n32_bit_compact_1_result[19], n32_bit_compact_1_result[20], n32_bit_compact_1_result[21], n32_bit_compact_1_result[22], n32_bit_compact_1_result[23]);
  nor nor_4 (nor_4_out, n32_bit_compact_1_result[24], n32_bit_compact_1_result[25], n32_bit_compact_1_result[26], n32_bit_compact_1_result[27], n32_bit_compact_1_result[28], n32_bit_compact_1_result[29], n32_bit_compact_1_result[30], n32_bit_compact_1_result[31]);
  and and_1 (eq, nor_1_out, nor_2_out, nor_3_out, nor_4_out);
endmodule

// HENC
module hamming_encoder (
  input  [25:0] data_input,
  output [4:0] parity,
  output security
);

  xor xor_1 (security, data_input[0], data_input[1], data_input[2], data_input[3], data_input[4], data_input[5], data_input[6], data_input[7], data_input[8], data_input[9], data_input[10], data_input[11], data_input[12], data_input[13], data_input[14], data_input[15], data_input[16], data_input[17], data_input[18], data_input[19], data_input[20], data_input[21], data_input[22], data_input[23], data_input[24], data_input[25], parity[0], parity[1], parity[2], parity[3], parity[4]);
  xor xor_2 (parity[0], data_input[0], data_input[1], data_input[3], data_input[4], data_input[6], data_input[8], data_input[10], data_input[11], data_input[13], data_input[15], data_input[17], data_input[19], data_input[21], data_input[23], data_input[25]);
  xor xor_3 (parity[1], data_input[0], data_input[2], data_input[3], data_input[5], data_input[6], data_input[9], data_input[10], data_input[12], data_input[13], data_input[16], data_input[17], data_input[20], data_input[21], data_input[24], data_input[25]);
  xor xor_4 (parity[2], data_input[1], data_input[2], data_input[3], data_input[7], data_input[8], data_input[9], data_input[10], data_input[14], data_input[15], data_input[16], data_input[17], data_input[22], data_input[23], data_input[24], data_input[25]);
  xor xor_5 (parity[3], data_input[4], data_input[5], data_input[6], data_input[7], data_input[8], data_input[9], data_input[10], data_input[18], data_input[19], data_input[20], data_input[21], data_input[22], data_input[23], data_input[24], data_input[25]);
  xor xor_6 (parity[4], data_input[11], data_input[12], data_input[13], data_input[14], data_input[15], data_input[16], data_input[17], data_input[18], data_input[19], data_input[20], data_input[21], data_input[22], data_input[23], data_input[24], data_input[25]);
endmodule

// HDEC
module hamming_decoder (
  input  [31:0] data_in,
  output [25:0] data_out,
  output error
);

  wire decoder_1_out0, xor_4_out, xor_5_out;
  wire [4:0] decoder_1_out1, hamming_encoder_1_parity, xor_1_out, xor_2_out;
  wire [25:0] decoder_1_out3;

  hamming_encoder hamming_encoder_1 (.data_input(data_in[25:0]), .parity(hamming_encoder_1_parity));  // open: security
  Decoder #(.select(5), .disabled(0), .enable("false")) decoder_1 (
    .out0(decoder_1_out0), .out1(decoder_1_out1[0]), .out2(decoder_1_out1[1]), .out3(decoder_1_out3[0]),
    .out4(decoder_1_out1[2]), .out5(decoder_1_out3[1]), .out6(decoder_1_out3[2]), .out7(decoder_1_out3[3]),
    .out8(decoder_1_out1[3]), .out9(decoder_1_out3[4]), .out10(decoder_1_out3[5]), .out11(decoder_1_out3[6]),
    .out12(decoder_1_out3[7]), .out13(decoder_1_out3[8]), .out14(decoder_1_out3[9]),
    .out15(decoder_1_out3[10]), .out16(decoder_1_out1[4]), .out17(decoder_1_out3[11]),
    .out18(decoder_1_out3[12]), .out19(decoder_1_out3[13]), .out20(decoder_1_out3[14]),
    .out21(decoder_1_out3[15]), .out22(decoder_1_out3[16]), .out23(decoder_1_out3[17]),
    .out24(decoder_1_out3[18]), .out25(decoder_1_out3[19]), .out26(decoder_1_out3[20]),
    .out27(decoder_1_out3[21]), .out28(decoder_1_out3[22]), .out29(decoder_1_out3[23]),
    .out30(decoder_1_out3[24]), .out31(decoder_1_out3[25]), .sel(xor_1_out));
  assign xor_1_out = hamming_encoder_1_parity ^ data_in[30:26];  // XOR_Gate xor_1, 5 bits wide
  assign xor_2_out = decoder_1_out1 ^ data_in[30:26];  // XOR_Gate xor_2, 5 bits wide
  assign data_out = data_in[25:0] ^ decoder_1_out3;  // XOR_Gate xor_3, 26 bits wide
  xor xor_4 (xor_4_out, data_out[0], data_out[1], data_out[2], data_out[3], data_out[4], data_out[5], data_out[6], data_out[7], data_out[8], data_out[9], data_out[10], data_out[11], data_out[12], data_out[13], data_out[14], data_out[15], data_out[16], data_out[17], data_out[18], data_out[19], data_out[20], data_out[21], data_out[22], data_out[23], data_out[24], data_out[25], xor_2_out[0], xor_2_out[1], xor_2_out[2], xor_2_out[3], xor_2_out[4]);
  xor xor_5 (xor_5_out, xor_4_out, data_in[31]);
  and and_1 (error, xor_5_out, ~decoder_1_out0);  // AND_Gate

  // Notes on the sheet:
  //   this wire is asserted if old data and old parity match
endmodule
